// Logisim project ALU.circ as structural Verilog: 1 circuit, main circuit ALU
module ALU (
  input  [15:0] Read_Reg_1,
  input  [15:0] Read_Reg_2,
  input  [3:0] ALU_OPR,
  input  [3:0] Shift_amount,
  output [15:0] ALU_OUT,
  output Zero_Flag,
  output Overflow
);

  wire [15:0] AU_OUT, LU_OUT, SH_OUT;

  AU au_1 (
    .in_1(ALU_OPR[3:2]), .in_2(Read_Reg_1), .in_3(Read_Reg_2), .out_4(AU_OUT), .out_5(Zero_Flag),
    .out_6(Overflow));
  LogicUnit logicunit_1 (.in_2(Read_Reg_2), .in_3(ALU_OPR[3:2]), .out_4(LU_OUT), .in_1(Read_Reg_1));
  shifter shifter_1 (.in_1(ALU_OPR[3:2]), .in_2(Read_Reg_1), .in_3(Shift_amount), .out_4(SH_OUT));
  Multiplexer #(.select(2), .width(16), .enable("false")) multiplexer_1 (
    .in0(LU_OUT), .in1(AU_OUT), .in2(SH_OUT), .out(ALU_OUT), .sel(ALU_OPR[1:0]));  // open: in3

  // Other names for the same wires on the sheet: OPR_Type[1:0] = ALU_OPR[1:0]; OPR[1:0] = ALU_OPR[3:2];
  //   BusA[15:0] = Read_Reg_1; BusB[15:0] = Read_Reg_2; OUT[15:0] = ALU_OUT
endmodule
