// Logisim project ArithmaticUnit.circ as structural Verilog: 2 circuits, main circuit 1- bit adder
module _1__bit_adder (
  input  in_1,
  input  in_2,
  input  in_3,
  input  in_4,
  output out_5,
  output out_6
);

  wire multiplexer_1_out, not_1_out;

  Multiplexer #(.enable("false")) multiplexer_1 (.in0(in_4), .in1(not_1_out), .out(multiplexer_1_out), .sel(in_1));
  not not_1 (not_1_out, in_4);
  Adder #(.width(1)) adder_1 (.a(in_3), .b(multiplexer_1_out), .out(out_5), .cin(in_2), .cout(out_6));

  // Other names for the same wires on the sheet: A = in_3; B = in_4; Binvert = in_1; c_out = out_6; carry_in = in_2;
  //   output = out_5
endmodule

module AU (
  input  [1:0] in_1,
  input  [15:0] in_2,
  input  [15:0] in_3,
  output [15:0] out_4,
  output out_5,
  output out_6
);

  wire c0, c1, c2, c3, c4, c5, c6, c7, c8, c9, c10, c11, c12, c13, c14, c15, not_2_out, o0, o1, o2, o3, o4,
       o5, o6, o7, o8, o9, o10, o11, o12, o13, o14, o15, or_2_out, Sub, xor_2_out;
  wire [15:0] SLT, SLTU;

  or or_1 (Sub, in_1[0], in_1[1]);
  _1__bit_adder u_1_bit_adder_1 (.in_1(Sub), .in_2(Sub), .in_3(in_2[0]), .in_4(in_3[0]), .out_5(o0), .out_6(c0));
  _1__bit_adder u_1_bit_adder_2 (.in_1(Sub), .in_2(c0), .in_3(in_2[1]), .in_4(in_3[1]), .out_5(o1), .out_6(c1));
  _1__bit_adder u_1_bit_adder_3 (.in_1(Sub), .in_2(c1), .in_3(in_2[2]), .in_4(in_3[2]), .out_5(o2), .out_6(c2));
  _1__bit_adder u_1_bit_adder_4 (.in_1(Sub), .in_2(c2), .in_3(in_2[3]), .in_4(in_3[3]), .out_5(o3), .out_6(c3));
  or or_2 (or_2_out, o0, o1, o2, o3, o4, o5, o6, o7, o8, o9, o10, o11, o12, o13, o14, o15);
  not not_1 (out_5, or_2_out);
  _1__bit_adder u_1_bit_adder_5 (.in_1(Sub), .in_2(c3), .in_3(in_2[4]), .in_4(in_3[4]), .out_5(o4), .out_6(c4));
  _1__bit_adder u_1_bit_adder_6 (.in_1(Sub), .in_2(c4), .in_3(in_2[5]), .in_4(in_3[5]), .out_5(o5), .out_6(c5));
  _1__bit_adder u_1_bit_adder_7 (.in_1(Sub), .in_2(c5), .in_3(in_2[6]), .in_4(in_3[6]), .out_5(o6), .out_6(c6));
  _1__bit_adder u_1_bit_adder_8 (.in_1(Sub), .in_2(c6), .in_3(in_2[7]), .in_4(in_3[7]), .out_5(o7), .out_6(c7));
  _1__bit_adder u_1_bit_adder_9 (.in_1(Sub), .in_2(c7), .in_3(in_2[8]), .in_4(in_3[8]), .out_5(o8), .out_6(c8));
  _1__bit_adder u_1_bit_adder_10 (.in_1(Sub), .in_2(c8), .in_3(in_2[9]), .in_4(in_3[9]), .out_5(o9), .out_6(c9));
  _1__bit_adder u_1_bit_adder_11 (.in_1(Sub), .in_2(c9), .in_3(in_2[10]), .in_4(in_3[10]), .out_5(o10), .out_6(c10));
  _1__bit_adder u_1_bit_adder_12 (.in_1(Sub), .in_2(c10), .in_3(in_2[11]), .in_4(in_3[11]), .out_5(o11), .out_6(c11));
  not not_2 (not_2_out, c15);
  xor xor_1 (out_6, c14, c15);
  xor xor_2 (xor_2_out, o15, out_6);
  assign SLT = {{15{1'b0}}, xor_2_out};  // Bit_Extender bit_extender_1
  assign SLTU = {{15{1'b0}}, not_2_out};  // Bit_Extender bit_extender_2
  _1__bit_adder u_1_bit_adder_13 (.in_1(Sub), .in_2(c11), .in_3(in_2[12]), .in_4(in_3[12]), .out_5(o12), .out_6(c12));
  _1__bit_adder u_1_bit_adder_14 (.in_1(Sub), .in_2(c12), .in_3(in_2[13]), .in_4(in_3[13]), .out_5(o13), .out_6(c13));
  _1__bit_adder u_1_bit_adder_15 (.in_1(Sub), .in_2(c13), .in_3(in_2[14]), .in_4(in_3[14]), .out_5(o14), .out_6(c14));
  _1__bit_adder u_1_bit_adder_16 (.in_1(Sub), .in_2(c14), .in_3(in_2[15]), .in_4(in_3[15]), .out_5(o15), .out_6(c15));
  Multiplexer #(.select(2), .width(16), .enable("false")) multiplexer_1 (
    .in0({o15, o14, o13, o12, o11, o10, o9, o8, o7, o6, o5, o4, o3, o2, o1, o0}),
    .in1({o15, o14, o13, o12, o11, o10, o9, o8, o7, o6, o5, o4, o3, o2, o1, o0}), .in2(SLT), .in3(SLTU),
    .out(out_4), .sel(in_1));

  // Other names for the same wires on the sheet: A[15:0] = in_2; a0 = in_2[0]; a1 = in_2[1]; a2 = in_2[2];
  //   a3 = in_2[3]; a4 = in_2[4]; a5 = in_2[5]; a6 = in_2[6]; a7 = in_2[7]; a8 = in_2[8]; a9 = in_2[9];
  //   a10 = in_2[10]; a11 = in_2[11]; a12 = in_2[12]; a13 = in_2[13]; a14 = in_2[14]; a15 = in_2[15]; B[15:0] = in_3;
  //   b0 = in_3[0]; b1 = in_3[1]; b2 = in_3[2]; b3 = in_3[3]; b4 = in_3[4]; b5 = in_3[5]; b6 = in_3[6]; b7 = in_3[7];
  //   b8 = in_3[8]; b9 = in_3[9]; b10 = in_3[10]; b11 = in_3[11]; b12 = in_3[12]; b13 = in_3[13]; b14 = in_3[14];
  //   b15 = in_3[15]; Opr[1:0] = in_1; OUT[15:0] = out_4; OverFlow = out_6;
  //   result[15:0] = {o15, o14, o13, o12, o11, o10, o9, o8, o7, o6, o5, o4, o3, o2, o1, o0}; zero = out_5
endmodule
