// Logisim project Shifter.circ as structural Verilog: 1 circuit, main circuit shifter
module shifter (
  input  [1:0] in_1,
  input  [15:0] in_2,
  input  [3:0] in_3,
  output [15:0] out_4
);

  wire [15:0] ROR, SLL, SRA, SRL;

  Shifter #(.width(16)) shifter_1 (.in(in_2), .\dist (in_3), .out(SLL));
  Shifter #(.width(16), .shift("lr")) shifter_2 (.in(in_2), .\dist (in_3), .out(SRL));
  Shifter #(.width(16), .shift("ar")) shifter_3 (.in(in_2), .\dist (in_3), .out(SRA));
  Shifter #(.width(16), .shift("rr")) shifter_4 (.in(in_2), .\dist (in_3), .out(ROR));
  Multiplexer #(.select(2), .width(16), .enable("false")) multiplexer_1 (
    .in0(SLL), .in1(SRL), .in2(SRA), .in3(ROR), .out(out_4), .sel(in_1));

  // Other names for the same wires on the sheet: input[15:0] = in_2; output[15:0] = out_4; shift_amount[3:0] = in_3;
  //   shift_control[1:0] = in_1
endmodule
