// Logisim project ALU.circ as structural Verilog: 2 circuits, main circuit ALU
module ALU (
  input  [3:0] in_1,
  input  [15:0] in_2,
  input  [15:0] in_3,
  input  [3:0] in_4,
  output [15:0] out_5,
  output out_6,
  output out_7
);

  wire [15:0] au_1_out_4, logicunit_1_out_4, main_1_out_4;

  LogicUnit logicunit_1 (.in_3(in_3), .out_4(logicunit_1_out_4), .in_2(in_2), .in_1(in_1[1:0]));
  shifter_main main_1 (.in_1(in_1[1:0]), .in_2(in_2), .in_3(in_4), .out_4(main_1_out_4));
  AU au_1 (.in_1(in_1[1:0]), .in_2(in_2), .in_3(in_3), .out_4(au_1_out_4), .out_5(out_7), .out_6(out_6));
  Multiplexer #(.select(2), .width(16), .enable("false")) multiplexer_1 (
    .in0(au_1_out_4), .in1(logicunit_1_out_4), .in2(main_1_out_4), .out(out_5), .sel(in_1[3:2]));  // open: in3

  // Other names for the same wires on the sheet: operation[1:0] = in_1[1:0]; selector[1:0] = in_1[3:2];
  //   input_1[15:0] = in_2; input_2[15:0] = in_3; output[15:0] = out_5; over_flow = out_7; shift_amount[3:0] = in_4;
  //   zero = out_6
endmodule

module Alu_test_bench (
);

  wire clock_1_out, clock_2_out;
  wire [6:0] counter_1_q;
  wire [7:0] rom_1_data;
  wire [15:0] alu_1_out_5, rom_2_data, rom_3_data;

  Clock clock_1 (.out(clock_1_out));
  Counter #(.width(7), .max('h7f)) counter_1 (
    .count(1'b1), .Q(counter_1_q), .clk(clock_1_out));  // open: load, D, carry, clr
  ROM #(.addrWidth(7)) rom_1 (.addr(counter_1_q), .data(rom_1_data), .sel(1'b1));
  ROM #(.addrWidth(7), .dataWidth(16)) rom_2 (.addr(counter_1_q), .data(rom_2_data), .sel(1'b1));
  ROM #(.addrWidth(7), .dataWidth(16)) rom_3 (.addr(counter_1_q), .data(rom_3_data), .sel(1'b1));
  ALU alu_1 (
    .in_1(rom_1_data[3:0]), .in_2(rom_2_data), .in_3(rom_3_data), .in_4(rom_3_data[3:0]), .out_5(alu_1_out_5));  // open: out_6, out_7
  Clock clock_2 (.out(clock_2_out));
  RAM #(.addrWidth(7), .dataWidth(16)) ram_1 (
    .addr(counter_1_q), .data(alu_1_out_5), .sel(1'b1), .clk(clock_2_out), .ld(1'b0));  // open: clr

  // Notes on the sheet:
  //   contents of rom_1 (hex, n*v repeats v):
  //   4 7 7 5 4 8 9 0 3 a 4 8 9 1 1 4 7 a 5 7 5 4 b 7 b 7 9 6 6 7 1 2 4 a a 5 4 6 9 3 7 3 6 7 4 9 7 b 3 a
  //   a b 3 1 4 1 6 0 7 b 0 0 6 0 3 9 0 9 b 4 a 6 7 0 3 1 5 2 2 9 5 9 2 7 9 2 7 9 6 b 9 3 0 a b 4 1 2 6 6
  //   8 1 1 1 b 7 6 b 8 5 5 a b 5 3 3 a 5 8 9 3 0 0 3 b 7
  //   contents of rom_2 (hex, n*v repeats v):
  //   728 c532 24fb 4ee6 2426 13a8 a4b5 5334 60d2 8be1 1e60 37c7 fdc 4969 5ff0 b7a9 77f2 aee3 a209 84df
  //   306 8528 1b6c bebc d12f 2b30 b31d 5e88 ceda 9da0 482d 7598 b002 dbbf 5f09 3bb9 f849 416e 870b 8ef8
  //   4f5d 5b72 2512 f37c 235f 6b93 7278 bace e9a0 c487 9c36 ada5 489 8534 320d 8c86 6065 e740 fab8 d12c
  //   5fc7 c383 69d6 fe77 cd30 ca5 7368 ea70 5c3 d427 c0c9 9557 f09a c855 3924 2d51 2373 a47b f939 e364
  //   1453 219 1278 7850 b3e1 12bb 7073 34a e212 51c2 d762 1f3e 4e32 29e3 791c 192b 5ecb 4557 b9f5 2c6f
  //   7519 2609 38ed 6ea8 9808 94c1 78f9 a863 d7e8 353b 5f18 5cd1 a6d1 8e13 e845 1ccd 7099 517d 3c06 abad
  //   b8b eeb 4889 5674 7e79 a67a 6c07
  //   contents of rom_3 (hex, n*v repeats v):
  //   cead 9356 88d8 5dd2 ed97 f b 824b 1282 e 2019 a 0 b1bb ed64 4d7b 829c 8 199b 2bcf 5ebf fd85 9 7431 c
  //   bea3 3 b384 f268 d339 22dd 674f fb83 b a 5b46 b25 476 3 24e0 4a27 fb79 be45 433c e1ee 2 4e68 6 6325
  //   2 a 1 c389 8382 a557 5e08 6af0 c34 575a 5 d2fd 4135 7ee5 6bc fb8 0 319a 3 0 f22b 7 328d 7dec b7f7
  //   2779 2768 3656 9ab5 525c c bbb1 0 2088 63a8 a eb4f 3fc8 4 88ab 9 5 c700 8d84 9 e 69b8 1eb2 f58f c8a3
  //   b285 7 8f32 dd2e 2220 d 44ee 559c a 2 51a6 38ef 9 5 8e3 695 4e6d 0 2d75 c 2 19f7 bac5 d478 d383 6
  //   d731 ba2d
endmodule
