// Logisim project Arithmatic Unit.circ as structural Verilog: 2 circuits, main circuit 1- bit adder
module _1__bit_adder (
  input  in_1,
  input  in_2,
  input  in_3,
  input  in_4,
  output out_5,
  output out_6
);

  wire multiplexer_1_out, not_1_out;

  Multiplexer #(.enable("false")) multiplexer_1 (.in0(in_4), .in1(not_1_out), .out(multiplexer_1_out), .sel(in_1));
  not not_1 (not_1_out, in_4);
  Adder #(.width(1)) adder_1 (.a(in_3), .b(multiplexer_1_out), .out(out_5), .cin(in_2), .cout(out_6));

  // Other names for the same wires on the sheet: A = in_3; B = in_4; Binvert = in_1; c_out = out_6; carry_in = in_2;
  //   output = out_5
endmodule

module AU (
  input  [1:0] in_1,
  input  [15:0] in_2,
  input  [15:0] in_3,
  output [15:0] out_4,
  output out_5,
  output out_6
);

  wire c14, c15, n1_bit_adder_1_out_6, n1_bit_adder_2_out_6, n1_bit_adder_3_out_6, n1_bit_adder_4_out_6,
       n1_bit_adder_5_out_6, n1_bit_adder_6_out_6, n1_bit_adder_7_out_6, n1_bit_adder_8_out_6,
       n1_bit_adder_9_out_6, n1_bit_adder_10_out_6, n1_bit_adder_11_out_6, n1_bit_adder_12_out_6,
       n1_bit_adder_13_out_6, n1_bit_adder_14_out_6, not_1_out, o0, o1, o2, o3, o4, o5, o6, o7, o8, o9, o10,
       o11, o12, o13, o14, o15, OPR, or_2_out, or_3_out, or_4_out, or_5_out, xor_1_out;
  wire [15:0] bit_extender_1_out, less;

  or or_1 (OPR, in_1[0], in_1[1]);
  not not_1 (not_1_out, c15);
  assign bit_extender_1_out = {{15{1'b0}}, not_1_out};  // Bit_Extender bit_extender_1
  xor xor_1 (xor_1_out, o15, out_5);
  Multiplexer #(.select(2), .width(16), .enable("false")) multiplexer_1 (
    .in0({o15, o14, o13, o12, o11, o10, o9, o8, o7, o6, o5, o4, o3, o2, o1, o0}),
    .in1({o15, o14, o13, o12, o11, o10, o9, o8, o7, o6, o5, o4, o3, o2, o1, o0}), .in2(less),
    .in3(bit_extender_1_out), .out(out_4), .sel(in_1));
  assign less = {{15{1'b0}}, xor_1_out};  // Bit_Extender bit_extender_2
  xor xor_2 (out_5, c14, c15);
  _1__bit_adder u_1_bit_adder_1 (
    .in_1(OPR), .in_2(OPR), .in_3(in_2[0]), .in_4(in_3[0]), .out_5(o0), .out_6(n1_bit_adder_1_out_6));
  _1__bit_adder u_1_bit_adder_2 (
    .in_1(OPR), .in_2(n1_bit_adder_1_out_6), .in_3(in_2[1]), .in_4(in_3[1]), .out_5(o1),
    .out_6(n1_bit_adder_2_out_6));
  _1__bit_adder u_1_bit_adder_3 (
    .in_1(OPR), .in_2(n1_bit_adder_2_out_6), .in_3(in_2[2]), .in_4(in_3[2]), .out_5(o2),
    .out_6(n1_bit_adder_3_out_6));
  _1__bit_adder u_1_bit_adder_4 (
    .in_1(OPR), .in_2(n1_bit_adder_3_out_6), .in_3(in_2[3]), .in_4(in_3[3]), .out_5(o3),
    .out_6(n1_bit_adder_4_out_6));
  _1__bit_adder u_1_bit_adder_5 (
    .in_1(OPR), .in_2(n1_bit_adder_4_out_6), .in_3(in_2[4]), .in_4(in_3[4]), .out_5(o4),
    .out_6(n1_bit_adder_5_out_6));
  _1__bit_adder u_1_bit_adder_6 (
    .in_1(OPR), .in_2(n1_bit_adder_5_out_6), .in_3(in_2[5]), .in_4(in_3[5]), .out_5(o5),
    .out_6(n1_bit_adder_6_out_6));
  _1__bit_adder u_1_bit_adder_7 (
    .in_1(OPR), .in_2(n1_bit_adder_6_out_6), .in_3(in_2[6]), .in_4(in_3[6]), .out_5(o6),
    .out_6(n1_bit_adder_7_out_6));
  _1__bit_adder u_1_bit_adder_8 (
    .in_1(OPR), .in_2(n1_bit_adder_7_out_6), .in_3(in_2[7]), .in_4(in_3[7]), .out_5(o7),
    .out_6(n1_bit_adder_8_out_6));
  or or_2 (or_2_out, o0, o1, o2, o3, o4);
  or or_3 (or_3_out, o5, o6, o7, o8, o9);
  or or_4 (or_4_out, o10, o11, o12, o13, o14);
  or or_5 (or_5_out, o15, or_4_out, or_3_out, or_2_out);
  not not_2 (out_6, or_5_out);
  _1__bit_adder u_1_bit_adder_9 (
    .in_1(OPR), .in_2(n1_bit_adder_8_out_6), .in_3(in_2[8]), .in_4(in_3[8]), .out_5(o8),
    .out_6(n1_bit_adder_9_out_6));
  _1__bit_adder u_1_bit_adder_10 (
    .in_1(OPR), .in_2(n1_bit_adder_9_out_6), .in_3(in_2[9]), .in_4(in_3[9]), .out_5(o9),
    .out_6(n1_bit_adder_10_out_6));
  _1__bit_adder u_1_bit_adder_11 (
    .in_1(OPR), .in_2(n1_bit_adder_10_out_6), .in_3(in_2[10]), .in_4(in_3[10]), .out_5(o10),
    .out_6(n1_bit_adder_11_out_6));
  _1__bit_adder u_1_bit_adder_12 (
    .in_1(OPR), .in_2(n1_bit_adder_11_out_6), .in_3(in_2[11]), .in_4(in_3[11]), .out_5(o11),
    .out_6(n1_bit_adder_12_out_6));
  _1__bit_adder u_1_bit_adder_13 (
    .in_1(OPR), .in_2(n1_bit_adder_12_out_6), .in_3(in_2[12]), .in_4(in_3[12]), .out_5(o12),
    .out_6(n1_bit_adder_13_out_6));
  _1__bit_adder u_1_bit_adder_14 (
    .in_1(OPR), .in_2(n1_bit_adder_13_out_6), .in_3(in_2[13]), .in_4(in_3[13]), .out_5(o13),
    .out_6(n1_bit_adder_14_out_6));
  _1__bit_adder u_1_bit_adder_15 (
    .in_1(OPR), .in_2(n1_bit_adder_14_out_6), .in_3(in_2[14]), .in_4(in_3[14]), .out_5(o14), .out_6(c14));
  _1__bit_adder u_1_bit_adder_16 (.in_1(OPR), .in_2(c14), .in_3(in_2[15]), .in_4(in_3[15]), .out_5(o15), .out_6(c15));

  // Other names for the same wires on the sheet: A[15:0] = in_2; a0 = in_2[0]; a1 = in_2[1]; a2 = in_2[2];
  //   a3 = in_2[3]; a4 = in_2[4]; a5 = in_2[5]; a6 = in_2[6]; a7 = in_2[7]; a8 = in_2[8]; a9 = in_2[9];
  //   a10 = in_2[10]; a11 = in_2[11]; a12 = in_2[12]; a13 = in_2[13]; a14 = in_2[14]; a15 = in_2[15]; B[15:0] = in_3;
  //   b0 = in_3[0]; b1 = in_3[1]; b2 = in_3[2]; b3 = in_3[3]; b4 = in_3[4]; b5 = in_3[5]; b6 = in_3[6]; b7 = in_3[7];
  //   b8 = in_3[8]; b9 = in_3[9]; b10 = in_3[10]; b11 = in_3[11]; b12 = in_3[12]; b13 = in_3[13]; b14 = in_3[14];
  //   b15 = in_3[15]; carry_out = c15; Output[15:0] = out_4; over_flow = out_5;
  //   result[15:0] = {o15, o14, o13, o12, o11, o10, o9, o8, o7, o6, o5, o4, o3, o2, o1, o0}; selector[1:0] = in_1;
  //   zero = out_6
endmodule
