// Logisim project Logical unit.circ as structural Verilog: 2 circuits, main circuit main
module main (
  input  [2:0] in_1,
  input  [15:0] in_2,
  input  [15:0] in_3,
  output [15:0] out_4
);

  _1__bit_Logical_Unit u_1_bit_logical_unit_1 (.in_1(in_1[1:0]), .in_2(in_2[0]), .in_3(in_3[0]), .out_4(out_4[0]));
  _1__bit_Logical_Unit u_1_bit_logical_unit_2 (.in_1(in_1[1:0]), .in_2(in_2[1]), .in_3(in_3[1]), .out_4(out_4[1]));
  _1__bit_Logical_Unit u_1_bit_logical_unit_3 (.in_1(in_1[1:0]), .in_2(in_2[2]), .in_3(in_3[2]), .out_4(out_4[2]));
  _1__bit_Logical_Unit u_1_bit_logical_unit_4 (.in_1(in_1[1:0]), .in_2(in_2[3]), .in_3(in_3[3]), .out_4(out_4[3]));
  _1__bit_Logical_Unit u_1_bit_logical_unit_5 (.in_1(in_1[1:0]), .in_2(in_2[4]), .in_3(in_3[4]), .out_4(out_4[4]));
  _1__bit_Logical_Unit u_1_bit_logical_unit_6 (.in_1(in_1[1:0]), .in_2(in_2[5]), .in_3(in_3[5]), .out_4(out_4[5]));
  _1__bit_Logical_Unit u_1_bit_logical_unit_7 (.in_1(in_1[1:0]), .in_2(in_2[6]), .in_3(in_3[6]), .out_4(out_4[6]));
  _1__bit_Logical_Unit u_1_bit_logical_unit_8 (.in_1(in_1[1:0]), .in_2(in_2[7]), .in_3(in_3[7]), .out_4(out_4[7]));
  _1__bit_Logical_Unit u_1_bit_logical_unit_9 (.in_1(in_1[1:0]), .in_2(in_2[12]), .in_3(in_3[12]), .out_4(out_4[12]));
  _1__bit_Logical_Unit u_1_bit_logical_unit_10 (.in_1(in_1[1:0]), .in_2(in_2[13]), .in_3(in_3[13]), .out_4(out_4[13]));
  _1__bit_Logical_Unit u_1_bit_logical_unit_11 (.in_1(in_1[1:0]), .in_2(in_2[14]), .in_3(in_3[14]), .out_4(out_4[14]));
  _1__bit_Logical_Unit u_1_bit_logical_unit_12 (.in_1(in_1[1:0]), .in_2(in_2[15]), .in_3(in_3[15]), .out_4(out_4[15]));
  _1__bit_Logical_Unit u_1_bit_logical_unit_13 (.in_1(in_1[1:0]), .in_2(in_2[8]), .in_3(in_3[8]), .out_4(out_4[8]));
  _1__bit_Logical_Unit u_1_bit_logical_unit_14 (.in_1(in_1[1:0]), .in_2(in_2[9]), .in_3(in_3[9]), .out_4(out_4[9]));
  _1__bit_Logical_Unit u_1_bit_logical_unit_15 (.in_1(in_1[1:0]), .in_2(in_2[10]), .in_3(in_3[10]), .out_4(out_4[10]));
  _1__bit_Logical_Unit u_1_bit_logical_unit_16 (.in_1(in_1[1:0]), .in_2(in_2[11]), .in_3(in_3[11]), .out_4(out_4[11]));

  // Other names for the same wires on the sheet: operation[1:0] = in_1[1:0]; _1__0 = in_2[0]; input_1[15:0] = in_2;
  //   _1__1 = in_2[1]; _1__2 = in_2[2]; _1__3 = in_2[3]; _1__4 = in_2[4]; _1__5 = in_2[5]; _1__6 = in_2[6];
  //   _1__7 = in_2[7]; _1__8 = in_2[8]; _1__9 = in_2[9]; _1__10 = in_2[10]; _1__11 = in_2[11]; _1__12 = in_2[12];
  //   _1__13 = in_2[13]; _1__14 = in_2[14]; _1__15 = in_2[15]; _2__0 = in_3[0]; input_2[15:0] = in_3; _2__1 = in_3[1];
  //   _2__2 = in_3[2]; _2__3 = in_3[3]; _2__4 = in_3[4]; _2__5 = in_3[5]; _2__6 = in_3[6]; _2__7 = in_3[7];
  //   _2__8 = in_3[8]; _2__9 = in_3[9]; _2__10 = in_3[10]; _2__11 = in_3[11]; _2__12 = in_3[12]; _2__13 = in_3[13];
  //   _2__14 = in_3[14]; _2__15 = in_3[15]; O_0 = out_4[0]; Output[15:0] = out_4; O_1 = out_4[1]; O_2 = out_4[2];
  //   O_3 = out_4[3]; O_4 = out_4[4]; O_5 = out_4[5]; O_6 = out_4[6]; O_7 = out_4[7]; O_8 = out_4[8]; O_9 = out_4[9];
  //   O_10 = out_4[10]; O_11 = out_4[11]; O_12 = out_4[12]; O_13 = out_4[13]; O_14 = out_4[14]; O_15 = out_4[15]
endmodule

module _1__bit_Logical_Unit (
  input  [1:0] in_1,
  input  in_2,
  input  in_3,
  output out_4
);

  wire and_1_out, not_1_out, or_1_out, xor_1_out;

  and and_1 (and_1_out, in_2, in_3);
  or or_1 (or_1_out, in_2, in_3);
  xor xor_1 (xor_1_out, in_2, in_3);
  not not_1 (not_1_out, or_1_out);
  Multiplexer #(.select(2)) multiplexer_1 (
    .in0(and_1_out), .in1(or_1_out), .in2(not_1_out), .in3(xor_1_out), .out(out_4), .sel(in_1));  // open: en

  // Other names for the same wires on the sheet: Input_1 = in_2; Input_2 = in_3; Logcal_1_bit_result = out_4;
  //   Operation[1:0] = in_1
endmodule
