// Logisim project ControlUnit.circ as structural Verilog: 4 circuits, main circuit PCcontrol
module ControlUnit (
  input  [4:0] OPcode,
  input  [1:0] F,
  output [3:0] PCsrc,
  output [3:0] ALUop,
  output [1:0] MemToReg,
  output MemWrite,
  output MemRead,
  output Ext_control,
  output ALUsrc,
  output RegWrite,
  output [1:0] RegDst
);

  PCcontrol pccontrol_1 (.OPcode(OPcode), .PCsrc(PCsrc));
  // ALUcontrol alucontrol_1: pin names not known; wires that end beside it: OPcode, F, ALUop
  OtherSignalsControl othersignalscontrol_1 (
    .OPcode(OPcode), .MemToReg(MemToReg), .MemWrite(MemWrite), .MemRead(MemRead), .Ext_control(Ext_control),
    .ALUsrc(ALUsrc), .RegWrite(RegWrite), .RegDst(RegDst));
endmodule

module PCcontrol (
  input  [4:0] OPcode,
  output [3:0] PCsrc
);

  wire and_1_out, and_2_out, and_3_out, and_4_out, and_5_out, not_2_out, not_3_out, not_4_out, not_5_out,
       not_6_out, not_7_out;

  not not_1 (PCsrc[3], OPcode[1]);
  not not_2 (not_2_out, OPcode[1]);
  not not_3 (not_3_out, OPcode[4]);
  not not_4 (not_4_out, OPcode[3]);
  not not_5 (not_5_out, OPcode[2]);
  not not_6 (not_6_out, OPcode[4]);
  not not_7 (not_7_out, OPcode[1]);
  and and_1 (and_1_out, OPcode[3], OPcode[2], OPcode[1]);
  or or_1 (PCsrc[1], and_1_out, and_2_out);
  and and_2 (and_2_out, OPcode[4], not_2_out);
  and and_3 (and_3_out, not_3_out, not_4_out, not_5_out, OPcode[1]);
  and and_4 (and_4_out, not_6_out, OPcode[3], OPcode[2], OPcode[1]);
  and and_5 (and_5_out, OPcode[4], not_7_out);
  or or_2 (PCsrc[0], and_3_out, and_4_out, and_5_out);

  assign PCsrc[2] = OPcode[0];

  // Other names for the same wires on the sheet: OP_1 = OPcode[1]; OP_2 = OPcode[2]; OP_3 = OPcode[3];
  //   OP_4 = OPcode[4]; PCsrc_0 = PCsrc[0]; PCsrc_1 = PCsrc[1]; OP_0 = OPcode[0]; PCsrc_2 = OPcode[0];
  //   PCsrc_3 = PCsrc[3]
endmodule

module ALUcontrol (
  input  [4:0] OPcode,
  input  [1:0] F,
  output [3:0] ALUop
);

  wire and_1_out, and_2_out, and_3_out, and_4_out, and_5_out, and_6_out, and_7_out, and_8_out, and_10_out,
       and_11_out, and_12_out, and_13_out, not_1_out, not_2_out, not_3_out, not_4_out, not_5_out, not_6_out,
       not_7_out, not_8_out, not_9_out, not_10_out, not_11_out, not_12_out, not_13_out, not_14_out,
       not_15_out, not_16_out, not_17_out, not_18_out, not_19_out, not_20_out;

  not not_1 (not_1_out, OPcode[3]);
  not not_2 (not_2_out, OPcode[2]);
  not not_3 (not_3_out, OPcode[1]);
  not not_4 (not_4_out, OPcode[2]);
  not not_5 (not_5_out, OPcode[3]);
  not not_6 (not_6_out, OPcode[0]);
  not not_7 (not_7_out, OPcode[2]);
  not not_8 (not_8_out, OPcode[4]);
  not not_9 (not_9_out, OPcode[3]);
  not not_10 (not_10_out, OPcode[2]);
  not not_11 (not_11_out, OPcode[1]);
  not not_12 (not_12_out, OPcode[3]);
  not not_13 (not_13_out, OPcode[1]);
  not not_14 (not_14_out, OPcode[2]);
  not not_15 (not_15_out, OPcode[2]);
  not not_16 (not_16_out, OPcode[3]);
  not not_17 (not_17_out, OPcode[2]);
  not not_18 (not_18_out, OPcode[3]);
  not not_19 (not_19_out, OPcode[2]);
  not not_20 (not_20_out, OPcode[3]);
  and and_1 (and_1_out, not_1_out, not_2_out, not_3_out, F[1]);
  and and_2 (and_2_out, not_4_out, OPcode[1], OPcode[0]);
  and and_3 (and_3_out, not_5_out, OPcode[2], OPcode[1], not_6_out);
  and and_4 (and_4_out, OPcode[3], not_7_out, OPcode[1]);
  and and_5 (and_5_out, not_8_out, not_9_out, not_10_out, not_11_out, F[0]);
  and and_6 (and_6_out, not_12_out, OPcode[2], not_13_out, OPcode[0]);
  and and_7 (and_7_out, OPcode[3], not_14_out, OPcode[0]);
  and and_8 (and_8_out, OPcode[3], OPcode[2], OPcode[1]);
  and and_9 (ALUop[1], OPcode[3], not_15_out);
  and and_10 (and_10_out, not_16_out, not_17_out, OPcode[0]);
  and and_11 (and_11_out, not_18_out, not_19_out, OPcode[1]);
  and and_12 (and_12_out, not_20_out, OPcode[1], OPcode[0]);
  and and_13 (and_13_out, OPcode[3], OPcode[2]);
  or or_1 (ALUop[3], and_1_out, and_2_out, and_3_out, and_4_out, OPcode[4]);
  or or_2 (ALUop[2], and_5_out, and_6_out, and_7_out, and_8_out);
  or or_3 (ALUop[0], and_10_out, and_11_out, and_12_out, and_13_out, OPcode[4]);

  // Other names for the same wires on the sheet: ALUop_0 = ALUop[0]; ALUop_1 = ALUop[1]; ALUop_2 = ALUop[2];
  //   ALUop_3 = ALUop[3]; F_0 = F[0]; F_1 = F[1]; OP_0 = OPcode[0]; OP_1 = OPcode[1]; OP_2 = OPcode[2];
  //   OP_3 = OPcode[3]; OP_4 = OPcode[4]
endmodule

module OtherSignalsControl (
  input  [4:0] OPcode,
  output [1:0] MemToReg,
  output MemWrite,
  output MemRead,
  output Ext_control,
  output ALUsrc,
  output RegWrite,
  output [1:0] RegDst
);

  wire and_2_out, and_5_out, and_6_out, and_7_out, and_8_out, and_9_out, and_10_out, and_11_out, and_12_out,
       and_13_out, and_14_out, and_15_out, not_1_out, not_2_out, not_3_out, not_4_out, not_5_out, not_6_out,
       not_7_out, not_8_out, not_9_out, not_10_out, not_11_out, not_12_out, not_13_out, not_14_out,
       not_15_out, not_16_out, not_17_out, not_18_out, not_19_out, not_20_out, not_21_out, not_22_out,
       not_23_out;

  and and_1 (MemToReg[0], OPcode[3], OPcode[2]);
  not not_1 (not_1_out, OPcode[4]);
  not not_2 (not_2_out, OPcode[1]);
  not not_3 (not_3_out, OPcode[4]);
  not not_4 (not_4_out, OPcode[1]);
  not not_5 (not_5_out, OPcode[0]);
  and and_2 (and_2_out, OPcode[1], OPcode[0]);
  not not_6 (not_6_out, OPcode[3]);
  not not_7 (not_7_out, OPcode[1]);
  not not_8 (not_8_out, OPcode[4]);
  not not_9 (not_9_out, OPcode[3]);
  not not_10 (not_10_out, OPcode[1]);
  not not_11 (not_11_out, OPcode[4]);
  not not_12 (not_12_out, OPcode[1]);
  not not_13 (not_13_out, OPcode[0]);
  not not_14 (not_14_out, OPcode[4]);
  not not_15 (not_15_out, OPcode[3]);
  not not_16 (not_16_out, OPcode[4]);
  not not_17 (not_17_out, OPcode[2]);
  not not_18 (not_18_out, OPcode[3]);
  not not_19 (not_19_out, OPcode[2]);
  not not_20 (not_20_out, OPcode[0]);
  not not_21 (not_21_out, OPcode[3]);
  not not_22 (not_22_out, OPcode[2]);
  not not_23 (not_23_out, OPcode[1]);
  and and_3 (MemWrite, not_1_out, OPcode[3], OPcode[2], not_2_out, OPcode[0]);
  and and_4 (MemRead, not_3_out, OPcode[3], OPcode[2], not_4_out, not_5_out);
  or or_1 (Ext_control, and_2_out, OPcode[3]);
  and and_5 (and_5_out, not_6_out, OPcode[2]);
  and and_6 (and_6_out, OPcode[3], not_7_out);
  and and_7 (and_7_out, OPcode[4], OPcode[1]);
  and and_8 (and_8_out, not_8_out, not_9_out, not_10_out);
  and and_9 (and_9_out, not_11_out, not_12_out, not_13_out);
  and and_10 (and_10_out, not_14_out, not_15_out, OPcode[2]);
  and and_11 (and_11_out, not_16_out, OPcode[3], not_17_out);
  and and_12 (and_12_out, OPcode[4], not_18_out, not_19_out, OPcode[1], not_20_out);
  and and_13 (and_13_out, OPcode[4], OPcode[3], OPcode[2], OPcode[1], OPcode[0]);
  and and_14 (and_14_out, not_21_out, not_22_out, not_23_out);
  and and_15 (and_15_out, OPcode[4], OPcode[3]);
  or or_2 (ALUsrc, and_5_out, and_6_out, and_7_out);
  or or_3 (RegWrite, and_8_out, and_9_out, and_10_out, and_11_out, and_12_out, and_13_out);
  or or_4 (RegDst[0], and_14_out, and_15_out);

  assign MemToReg[1] = OPcode[4];
  assign RegDst[1] = OPcode[4];

  // Other names for the same wires on the sheet: MemToReg_0 = MemToReg[0]; OP_0 = OPcode[0]; OP_1 = OPcode[1];
  //   OP_2 = OPcode[2]; OP_3 = OPcode[3]; RegDst_0 = RegDst[0]; MemToReg_1 = OPcode[4]; OP_4 = OPcode[4];
  //   RegDst_1 = OPcode[4]
endmodule
