// Logisim project DataMemory.circ as structural Verilog: 1 circuit, main circuit Data Memory
module Data_Memory (
  input  [15:0] Address,
  input  [15:0] Data_In,
  input  MemWrite,
  input  MemRead,
  input  CLK,
  output [15:0] Data_Out
);

  RAM #(.addrWidth(16), .dataWidth(16), .bus("separate")) ram_1 (
    .addr(Address), .din(Data_In), .data(Data_Out), .str(MemWrite), .sel(1'b1), .clk(CLK), .ld(MemRead),
    .clr(1'b0));
endmodule
