// Logisim project PC Control.circ as structural Verilog: 2 circuits, main circuit main
module main (
  input  [15:0] in_1,
  input  [3:0] in_2,
  input  in_3,
  input  [15:0] ALU_result,
  input  [10:0] in_5,
  input  [4:0] in_6,
  output [15:0] out_7
);

  wire [15:0] adder_1_out, adder_2_out, Brach_Control_out_6, Immi_5, Immi_11;

  assign Immi_11 = {{5{in_5[10]}}, in_5};  // Bit_Extender bit_extender_1
  assign Immi_5 = {{11{in_6[4]}}, in_6};  // Bit_Extender bit_extender_2
  Adder #(.width(16)) adder_1 (.a(in_1), .b(16'h1), .out(adder_1_out));  // open: cin, cout
  Adder #(.width(16)) adder_2 (.a(in_1), .b(Immi_11), .out(adder_2_out));  // open: cin, cout
  Branch_Control Brach_Control (
    .in_2(in_3), .in_3(ALU_result[0]), .in_1(in_1), .in_4(Immi_5), .out_6(Brach_Control_out_6),
    .in_5(in_2[3:2]));
  Multiplexer #(.select(2), .width(16), .enable("false")) multiplexer_1 (
    .in0(adder_1_out), .in1(ALU_result), .in2(adder_2_out), .in3(Brach_Control_out_6), .out(out_7),
    .sel(in_2[1:0]));

  // Other names for the same wires on the sheet: SLT_Flag = ALU_result[0]; Current_PC[15:0] = in_1;
  //   PC_Src[1:0] = in_2[1:0]; Branch_Op[1:0] = in_2[3:2]; Next_PC[15:0] = out_7; Zero_Flag = in_3
endmodule

module Branch_Control (
  input  [15:0] in_1,
  input  in_2,
  input  in_3,
  input  [15:0] in_4,
  input  [1:0] in_5,
  output [15:0] out_6
);

  wire not_1_out, not_2_out;
  wire [15:0] adder_1_out, adder_2_out, multiplexer_1_out, multiplexer_2_out, multiplexer_3_out,
       multiplexer_4_out;

  Adder #(.width(16)) adder_1 (.a(in_1), .b(16'h1), .out(adder_1_out));  // open: cin, cout
  Adder #(.width(16)) adder_2 (.a(in_1), .b(in_4), .out(adder_2_out));  // open: cin, cout
  Multiplexer #(.width(16), .enable("false")) multiplexer_1 (
    .in0(adder_1_out), .in1(adder_2_out), .out(multiplexer_1_out), .sel(in_2));
  not not_1 (not_1_out, in_2);
  Multiplexer #(.width(16), .enable("false")) multiplexer_2 (
    .in0(adder_1_out), .in1(adder_2_out), .out(multiplexer_2_out), .sel(not_1_out));
  Multiplexer #(.width(16), .enable("false")) multiplexer_3 (
    .in0(adder_1_out), .in1(adder_2_out), .out(multiplexer_3_out), .sel(in_3));
  not not_2 (not_2_out, in_3);
  Multiplexer #(.width(16), .enable("false")) multiplexer_4 (
    .in0(adder_1_out), .in1(adder_2_out), .out(multiplexer_4_out), .sel(not_2_out));
  Multiplexer #(.select(2), .width(16), .enable("false")) multiplexer_5 (
    .in0(multiplexer_1_out), .in1(multiplexer_2_out), .in2(multiplexer_3_out), .in3(multiplexer_4_out),
    .out(out_6), .sel(in_5));

  // Other names for the same wires on the sheet: Branch_Op[1:0] = in_5; Current_PC[15:0] = in_1;
  //   Immi_Value[15:0] = in_4; Next_PC[15:0] = out_6; SLT_Flag = in_3; Zero_Flag = in_2
endmodule
