// Logisim project PC_Control.circ as structural Verilog: 3 circuits, main circuit PC
module PC (
  input  [4:0] Imm_5,
  input  Zero_flag,
  input  in_3,
  input  [10:0] Imm_11,
  input  [3:0] PCsrc,
  input  [15:0] ALU_OUT,
  output [15:0] PC,
  output [15:0] PC_1
);

  wire [15:0] BC_OUT, JC_OUT, multiplexer_1_out;

  BranchControl branchcontrol_1 (
    .Imm_5(Imm_5), .Curr_PC(PC), .PC_1(PC_1), .Zero_flag(Zero_flag), .SLT_OUT(ALU_OUT[0]), .OPR(PCsrc[3:2]),
    .Next_Inst(BC_OUT));
  Multiplexer #(.select(2), .width(16), .enable("false")) multiplexer_1 (
    .in0(PC_1), .in1(ALU_OUT), .in2(JC_OUT), .in3(BC_OUT), .out(multiplexer_1_out), .sel(PCsrc[1:0]));
  Register #(.width(16)) u_PC (.D(multiplexer_1_out), .en(1'b1), .Q(PC), .clk(in_3), .clr(1'b0));
  Adder #(.width(16)) adder_1 (.a({16{1'b0}}), .b(PC), .out(PC_1), .cin(1'b1));  // open: cout
  JumpControl jumpcontrol_1 (.Imm_11(Imm_11), .PC(PC), .out_3(JC_OUT));

  // Other names for the same wires on the sheet: CLK = in_3; OPR[1:0] = PCsrc[1:0]; B_OPR[1:0] = PCsrc[3:2];
  //   Less = ALU_OUT[0]; Rs[15:0] = ALU_OUT; Zero = Zero_flag
endmodule

module BranchControl (
  input  [4:0] Imm_5,
  input  [15:0] Curr_PC,
  input  [15:0] PC_1,
  input  Zero_flag,
  input  SLT_OUT,
  input  [1:0] OPR,
  output [15:0] Next_Inst
);

  wire [15:0] Address, BEQ, BGE, BLT, BNE, Ext_Imm_5;

  Multiplexer #(.width(16), .enable("false")) multiplexer_1 (.in0(PC_1), .in1(Address), .out(BEQ), .sel(Zero_flag));
  Multiplexer #(.select(2), .width(16), .enable("false")) multiplexer_2 (
    .in0(BEQ), .in1(BNE), .in2(BLT), .in3(BGE), .out(Next_Inst), .sel(OPR));
  Multiplexer #(.width(16), .enable("false")) multiplexer_3 (.in0(Address), .in1(PC_1), .out(BNE), .sel(Zero_flag));
  assign Ext_Imm_5 = {{11{Imm_5[4]}}, Imm_5};  // Bit_Extender bit_extender_1
  Adder #(.width(16)) adder_1 (.a(Ext_Imm_5), .b(Curr_PC), .out(Address), .cin(1'b0));  // open: cout
  Multiplexer #(.width(16), .enable("false")) multiplexer_4 (.in0(PC_1), .in1(Address), .out(BLT), .sel(SLT_OUT));
  Multiplexer #(.width(16), .enable("false")) multiplexer_5 (.in0(Address), .in1(PC_1), .out(BGE), .sel(SLT_OUT));

  // Other names for the same wires on the sheet: Less = SLT_OUT; PC[15:0] = Curr_PC; Zero = Zero_flag
endmodule

module JumpControl (
  input  [10:0] Imm_11,
  input  [15:0] PC,
  output [15:0] out_3
);

  wire [15:0] Ext_Imm_11;

  assign Ext_Imm_11 = {{5{Imm_11[10]}}, Imm_11};  // Bit_Extender bit_extender_1
  Adder #(.width(16)) adder_1 (.a(Ext_Imm_11), .b(PC), .out(out_3), .cin(1'b0));  // open: cout

  // Other names for the same wires on the sheet: Next_Inst[15:0] = out_3
endmodule
