// Logisim project Branch and J Forward.circ as structural Verilog: 5 circuits, main circuit MEM->ID Forward
module Branch_J_Forward (
  input  in_1,
  input  in_2,
  input  in_3,
  input  in_4,
  input  in_5,
  input  [2:0] in_6,
  input  [2:0] in_7,
  input  [2:0] in_8,
  input  [2:0] in_9,
  input  [2:0] in_10,
  output out_11,
  output out_12,
  output [1:0] out_13,
  output [1:0] out_14
);

  wire ForwardC_MEM, ForwardC_WB, ForwardD_MEM, ForwardD_WB, stall_load_Mem;

  or or_1 (out_11, out_12, stall_load_Mem);
  Calc_FC_FD calc_fc_fd_1 (.MEM(ForwardC_MEM), .F1(out_13[1]), .F0(out_13[0]), .WB(ForwardC_WB));
  Calc_FC_FD calc_fc_fd_2 (.MEM(ForwardD_MEM), .F1(out_14[1]), .F0(out_14[0]), .WB(ForwardD_WB));
  EX__ID_Forward ex_id_forward_1 (.in_1(in_1), .in_3(in_6), .in_4(in_9), .in_5(in_10), .out_6(out_12), .in_2(in_2));
  MEM__ID_Forward mem_id_forward_1 (
    .in_1(in_1), .in_3(in_7), .in_4(in_9), .in_5(in_10), .out_7(ForwardC_MEM), .out_8(ForwardD_MEM),
    .in_2(in_3), .in_6(in_5), .out_9(stall_load_Mem));
  WB__ID_Forward wb_id_forward_1 (
    .in_1(in_1), .in_3(in_8), .in_4(in_9), .in_5(in_10), .out_6(ForwardC_WB), .out_7(ForwardD_WB), .in_2(in_4));

  // Other names for the same wires on the sheet: Branch = in_1; EX_MEM_Rd[2:0] = in_7; Ex_stall = out_12;
  //   ForwardC[1:0] = out_13; ForwardD[1:0] = out_14; ID_EX_Rd[2:0] = in_6; IF_ID_Rs[2:0] = in_9;
  //   IF_ID_Rt[2:0] = in_10; MEM_WB_Rd[2:0] = in_8; MemRead_Mem = in_5; RegWrite_EX = in_2; RegWrite_MEM = in_3;
  //   RegWrite_WB = in_4
endmodule

module EX__ID_Forward (
  input  in_1,
  input  in_2,
  input  [2:0] in_3,
  input  [2:0] in_4,
  input  [2:0] in_5,
  output out_6
);

  wire and_1_out, and_2_out, nR0, Rd__Rs, Rd__Rt;

  and and_1 (and_1_out, in_1, in_2, nR0, Rd__Rs);
  and and_2 (and_2_out, in_1, in_2, nR0, Rd__Rt);
  or or_1 (nR0, in_3[0], in_3[1], in_3[2]);
  Comparator #(.width(3)) comparator_1 (.a(in_3), .b(in_4), .eq(Rd__Rs));  // open: gt, lt
  Comparator #(.width(3)) comparator_2 (.a(in_3), .b(in_5), .eq(Rd__Rt));  // open: gt, lt
  or or_2 (out_6, and_1_out, and_2_out);

  // Other names for the same wires on the sheet: Branch = in_1; EX_Rd[2:0] = in_3; ID_Rs[2:0] = in_4;
  //   ID_Rt[2:0] = in_5; RegWrite_EX = in_2; Stall_Branch = out_6
endmodule

module MEM__ID_Forward (
  input  in_1,
  input  in_2,
  input  [2:0] in_3,
  input  [2:0] in_4,
  input  [2:0] in_5,
  input  in_6,
  output out_7,
  output out_8,
  output out_9
);

  wire and_2_out, and_3_out, nR0, Rd__Rs, Rd__Rt;

  and and_1 (out_7, in_1, in_2, nR0, Rd__Rs);
  or or_1 (nR0, in_3[0], in_3[1], in_3[2]);
  Comparator #(.width(3)) comparator_1 (.a(in_3), .b(in_4), .eq(Rd__Rs));  // open: gt, lt
  Comparator #(.width(3)) comparator_2 (.a(in_3), .b(in_5), .eq(Rd__Rt));  // open: gt, lt
  and and_2 (and_2_out, in_6, out_7);
  and and_3 (and_3_out, in_6, out_8);
  or or_2 (out_9, and_2_out, and_3_out);
  and and_4 (out_8, in_1, in_2, nR0, Rd__Rt);

  // Other names for the same wires on the sheet: Branch = in_1; ForwardC_MEM = out_7; ForwardD_MEM = out_8;
  //   ID_Rs[2:0] = in_4; ID_Rt[2:0] = in_5; MEM_Rd[2:0] = in_3; MemRead_Mem = in_6; RegWrite_MEM = in_2;
  //   Stall_Branch = out_9
endmodule

module WB__ID_Forward (
  input  in_1,
  input  in_2,
  input  [2:0] in_3,
  input  [2:0] in_4,
  input  [2:0] in_5,
  output out_6,
  output out_7
);

  wire nR0, Rd__Rs, Rd__Rt;

  and and_1 (out_6, in_1, in_2, nR0, Rd__Rs);
  or or_1 (nR0, in_3[0], in_3[1], in_3[2]);
  Comparator #(.width(3)) comparator_1 (.a(in_3), .b(in_4), .eq(Rd__Rs));  // open: gt, lt
  Comparator #(.width(3)) comparator_2 (.a(in_3), .b(in_5), .eq(Rd__Rt));  // open: gt, lt
  and and_2 (out_7, in_1, in_2, nR0, Rd__Rt);

  // Other names for the same wires on the sheet: Branch = in_1; ForwardC_WB = out_6; ForwardD_WB = out_7;
  //   ID_Rs[2:0] = in_4; ID_Rt[2:0] = in_5; RegWrite_WB = in_2; WB_Rd[2:0] = in_3
endmodule

module Calc_FC_FD (
  input  MEM,
  input  WB,
  output F1,
  output F0
);

  wire not_1_out;

  not not_1 (not_1_out, MEM);
  and and_1 (F1, not_1_out, WB);

  assign F0 = MEM;
endmodule
