// Logisim project Full Circuit.circ as structural Verilog: 1 circuit, main circuit Full Circuit
module Full_Circuit (
);

  wire ALUsrc_Ex, ALUsrc_Id, Branch_J_Kill, CLK, Ext_Control_Ex, Ext_Control_Id, MemRead_Ex, MemRead_Id,
       MemRead_Mem, MemWrite_Ex, MemWrite_Id, MemWrite_Mem, multiplexer_6_out, multiplexer_7_out,
       multiplexer_8_out, not_1_out, not_2_out, or_1_out, Overflow, RegWrite_Ex, RegWrite_Id, RegWrite_Mem,
       RegWrite_Wb, stall, zero;
  wire [1:0] F_Id, Forward_A, Forward_B, ForwardC, ForwardD, MemToReg_Ex, MemToReg_Id, MemToReg_Mem,
       MemToReg_Wb, RegDst_Signal_Id;
  wire [2:0] Rd_Id, RegDes_Ex, RegDes_Id, RegDes_Mem, RegDes_Wb, Rs_Ex, Rs_Id, Rs_Mem, Rt_Ex, Rt_Id, Rt_Id_t,
       Rt_Mem;
  wire [3:0] ALUop_Ex, ALUop_Id, PCsrc_Id, Shift_Amount_Ex, Shift_Amount_Id;
  wire [4:0] Imm_5_Id, OP_Id;
  wire [10:0] Imm_11_Id;
  wire [15:0] ALU_out_Ex, bit_extender_1_out, EX_Result, Ex_Result_Mem, Ex_Result_Wb, Ext_Out_Ex, Ext_Out_Id,
       Imm_11__5_Ex, Imm_11__5_Id, Imm_11__5_Mem, Imm_11__5_Wb, ins, Mem_out_Mem, Mem_out_Wb, MEM_Result,
       multiplexer_1_out, multiplexer_2_out, multiplexer_4_out, multiplexer_5_out, multiplexer_10_out,
       multiplexer_11_out, New_Rt_Data_Ex, Next_PC, PC_1_Ex, PC_1_Id, PC_1_If, PC_1_Mem, PC_1_Wb, PC_Id,
       PC_If, R1, R2, R3, R4, R5, R6, R7, reg_if_id_1_instruction, Rs_Data_Ex, Rs_Data_Id, Rs_Data_Mem,
       Rt_Data_Ex, Rt_Data_Id, Rt_Data_Mem, Write_Data;

  Clock clock_1 (.out(CLK));
  Adder #(.width(16)) adder_1 (.a(PC_If), .b(16'h1), .out(PC_1_If));  // open: cin, cout
  // Probe on R1
  // Probe on R2
  // Probe on R3
  // Probe on R4
  // Probe on R5
  // Probe on R6
  // Probe on R7
  // Probe on PC_If
  // Probe on ins
  Multiplexer #(.width(16), .enable("false")) multiplexer_1 (
    .in0(PC_1_If), .in1(Next_PC), .out(multiplexer_1_out), .sel(Branch_J_Kill));
  // Probe on R1
  // Probe on R2
  // Probe on R3
  // Probe on R4
  // Probe on R5
  // Probe on R6
  // Probe on R7
  Register #(.width(16)) PC (.D(multiplexer_1_out), .en(not_1_out), .Q(PC_If), .clk(CLK), .clr(1'b0));
  not not_1 (not_1_out, stall);
  ROM #(.addrWidth(16), .dataWidth(16)) rom_1 (.addr(PC_If), .data(ins), .sel(1'b1));
  Multiplexer #(.width(16), .enable("false")) multiplexer_2 (
    .in0(ins), .in1({16{1'b0}}), .out(multiplexer_2_out), .sel(Branch_J_Kill));
  Reg_If_Id reg_if_id_1 (
    .in_3(multiplexer_2_out), .Instruction(reg_if_id_1_instruction), .in_1(CLK), .in_4(PC_1_If),
    .PC_1(PC_1_Id), .in_5(PC_If), .PC(PC_Id), .in_2(stall));
  InstructionDecoder instructiondecoder_1 (
    .Instruction(reg_if_id_1_instruction), .out_2(Rt_Id_t), .out_3(Rs_Id), .out_4(Rd_Id), .out_5(F_Id),
    .out_6(OP_Id), .out_7(Imm_5_Id), .out_9(Imm_11_Id), .out_8(Shift_Amount_Id));
  Multiplexer #(.select(2), .width(3), .enable("false")) multiplexer_3 (
    .in0(Rt_Id_t), .in1(Rd_Id), .in2(3'b001), .in3(3'b111), .out(RegDes_Id), .sel(RegDst_Signal_Id));
  Control_Unit control_unit_1 (
    .in_1(OP_Id), .in_2(F_Id), .out_4(ALUsrc_Id), .out_3(ALUop_Id), .out_5(MemRead_Id), .out_6(MemWrite_Id),
    .out_7(Ext_Control_Id), .out_8(MemToReg_Id), .out_9(RegWrite_Id), .out_10(RegDst_Signal_Id),
    .out_11(PCsrc_Id));
  not not_2 (not_2_out, CLK);
  Hazard_Detection_Unit hazard_detection_unit_1 (
    .in_1(Rs_Id), .in_2(Rt_Id_t), .in_3(Rt_Ex), .in_4(MemRead_Ex), .out_6(stall), .in_5(MemRead_Id));
  RegFile regfile_1 (
    .out_7(Rs_Data_Id), .in_2(Rs_Id), .in_6(not_2_out), .out_8(Rt_Data_Id), .in_3(Rt_Id_t),
    .in_5(RegWrite_Wb), .in_4(RegDes_Wb), .in_1(Write_Data), .out_9(R1), .out_10(R2), .out_11(R3),
    .out_12(R4), .out_13(R5), .out_14(R6), .out_15(R7));
  Multiplexer #(.select(2), .width(16), .enable("false")) multiplexer_4 (
    .in0(Rt_Data_Id), .in1(EX_Result), .in2(MEM_Result), .in3(Write_Data), .out(multiplexer_4_out),
    .sel(ForwardD));
  Multiplexer #(.select(2), .width(16), .enable("false")) multiplexer_5 (
    .in0(Rs_Data_Id), .in1(EX_Result), .in2(MEM_Result), .in3(Write_Data), .out(multiplexer_5_out),
    .sel(ForwardC));
  assign bit_extender_1_out = {{5{1'b0}}, Imm_11_Id};  // Bit_Extender bit_extender_1
  Shifter #(.width(16)) shifter_1 (.in(bit_extender_1_out), .\dist (4'b0101), .out(Imm_11__5_Id));
  or or_1 (or_1_out, PCsrc_Id[0], PCsrc_Id[1]);
  Extender extender_1 (.in_1(Ext_Control_Id), .in_2(Imm_5_Id), .out_3(Ext_Out_Id));
  PC_control pc_control_1 (
    .in_1(PC_Id), .in_2(PCsrc_Id), .in_5(Imm_11_Id), .in_6(Imm_5_Id), .out_7(Next_PC),
    .in_3(multiplexer_5_out), .in_4(multiplexer_4_out), .out_8(Branch_J_Kill));
  // Branch_J_Forward branch_j_forward_1: pin names not known; wires that end beside it: RegDes_Ex, RegDes_Mem, RegDes_Wb, or_1_out, Rs_Id, RegWrite_Ex, RegWrite_Mem, Rt_Id, RegWrite_Wb, ForwardC, ForwardD
  Multiplexer #(.enable("false")) multiplexer_6 (.in0(MemRead_Id), .in1(1'b0), .out(multiplexer_6_out), .sel(stall));
  Multiplexer #(.enable("false")) multiplexer_7 (.in0(MemWrite_Id), .in1(1'b0), .out(multiplexer_7_out), .sel(stall));
  Multiplexer #(.enable("false")) multiplexer_8 (.in0(RegWrite_Id), .in1(1'b0), .out(multiplexer_8_out), .sel(stall));
  Reg_Id_Ex reg_id_ex_1 (
    .in_4(ALUop_Id), .in_5(ALUsrc_Id), .in_7(multiplexer_6_out), .in_8(multiplexer_7_out),
    .in_12(Ext_Control_Id), .in_13(MemToReg_Id), .in_16(Rs_Data_Id), .in_15(Rt_Data_Id), .out_20(ALUop_Ex),
    .out_21(ALUsrc_Ex), .out_23(MemRead_Ex), .out_24(MemWrite_Ex), .out_28(Ext_Control_Ex),
    .out_29(MemToReg_Ex), .out_32(Rs_Data_Ex), .out_31(Rt_Data_Ex), .in_1(CLK), .in_14(Rs_Id),
    .out_30(Rs_Ex), .in_9(Rt_Id_t), .out_25(Rt_Ex), .in_17(RegDes_Id), .out_33(RegDes_Ex),
    .in_11(multiplexer_8_out), .out_27(RegWrite_Ex), .in_6(Ext_Out_Id), .out_22(Ext_Out_Ex),
    .in_3(Shift_Amount_Id), .out_19(Shift_Amount_Ex), .in_10(Imm_11__5_Id), .out_26(Imm_11__5_Ex),
    .in_2(PC_1_Id), .out_18(PC_1_Ex));
  Multiplexer #(.select(2), .width(16), .enable("false")) multiplexer_9 (
    .in0(Rt_Data_Ex), .in1(Write_Data), .in2(Ex_Result_Mem), .out(New_Rt_Data_Ex), .sel(Forward_B));  // open: in3
  Multiplexer #(.width(16), .enable("false")) multiplexer_10 (
    .in0(New_Rt_Data_Ex), .in1(Ext_Out_Ex), .out(multiplexer_10_out), .sel(ALUsrc_Ex));
  Multiplexer #(.select(2), .width(16), .enable("false")) multiplexer_11 (
    .in0(Rs_Data_Ex), .in1(Write_Data), .in2(Ex_Result_Mem), .out(multiplexer_11_out), .sel(Forward_A));  // open: in3
  ALU alu_1 (
    .in_1(ALUop_Ex), .in_2(multiplexer_11_out), .in_3(multiplexer_10_out), .in_4(Shift_Amount_Ex),
    .out_5(ALU_out_Ex), .out_6(zero), .out_7(Overflow));
  Forwarding_Unit forwarding_unit_1 (
    .in_1(Rs_Ex), .in_2(Rt_Ex), .in_3(RegWrite_Mem), .in_4(RegDes_Mem), .in_5(RegWrite_Wb), .in_6(RegDes_Wb),
    .out_7(Forward_A), .out_8(Forward_B));
  Multiplexer #(.select(2), .width(16), .enable("false")) multiplexer_12 (
    .in0(ALU_out_Ex), .in1(ALU_out_Ex), .in2(Imm_11__5_Ex), .in3(PC_1_Ex), .out(EX_Result), .sel(MemToReg_Ex));
  Reg_Ex_Mem reg_ex_mem_1 (
    .in_1(CLK), .in_2(MemRead_Ex), .in_3(MemWrite_Ex), .in_4(New_Rt_Data_Ex), .in_5(MemToReg_Ex),
    .in_6(Rs_Data_Ex), .in_8(RegWrite_Ex), .in_9(Rs_Ex), .in_10(Rt_Ex), .in_11(RegDes_Ex),
    .out_14(MemRead_Mem), .out_15(MemWrite_Mem), .out_16(Rt_Data_Mem), .out_17(MemToReg_Mem),
    .out_18(Rs_Data_Mem), .out_20(RegWrite_Mem), .out_21(Rs_Mem), .out_22(Rt_Mem), .out_23(RegDes_Mem),
    .in_7(EX_Result), .out_19(Ex_Result_Mem), .in_12(PC_1_Ex), .out_24(PC_1_Mem), .in_13(Imm_11__5_Ex),
    .out_25(Imm_11__5_Mem));
  Data_Memory data_memory_1 (
    .Address(Ex_Result_Mem), .Data_In(Rt_Data_Mem), .MemWrite(MemWrite_Mem), .MemRead(MemRead_Mem),
    .CLK(CLK), .Data_Out(Mem_out_Mem));
  Multiplexer #(.width(16), .enable("false")) multiplexer_13 (
    .in0(Ex_Result_Mem), .in1(Mem_out_Mem), .out(MEM_Result), .sel(MemRead_Mem));
  Reg_Mem_Wb reg_mem_wb_1 (
    .in_1(CLK), .in_2(MemToReg_Mem), .in_5(Ex_Result_Mem), .in_6(PC_1_Mem), .in_7(Imm_11__5_Mem),
    .in_8(Mem_out_Mem), .out_9(MemToReg_Wb), .out_12(Ex_Result_Wb), .out_13(PC_1_Wb), .out_14(Imm_11__5_Wb),
    .out_15(Mem_out_Wb), .in_3(RegWrite_Mem), .out_10(RegWrite_Wb), .in_4(RegDes_Mem), .out_11(RegDes_Wb));
  Multiplexer #(.select(2), .width(16), .enable("false")) multiplexer_14 (
    .in0(Ex_Result_Wb), .in1(Mem_out_Wb), .in2(Imm_11__5_Wb), .in3(PC_1_Wb), .out(Write_Data),
    .sel(MemToReg_Wb));

  // Notes on the sheet:
  //   contents of rom_1 (hex, n*v repeats v):
  //   9384 3b4d 4cd 6001 6042 6083 3aa4 b24 914 d93 70f0 88a 7700 6804 f804 4193 58de 77c0 353 6001 614a
  //   618b 113 6804 1038
endmodule
