// Logisim project Hazard Detection Unit.circ as structural Verilog: 1 circuit, main circuit Hazard Detection Unit
module Hazard_Detection_Unit (
  input  [2:0] in_1,
  input  [2:0] in_2,
  input  [2:0] in_3,
  input  in_4,
  input  in_5,
  output out_6
);

  wire and_1_out, not_1_out, or_1_out, Rs____Rt__Ex, Rt____Rt__Ex;

  not not_1 (not_1_out, in_5);
  and and_1 (and_1_out, not_1_out, Rt____Rt__Ex);
  Comparator #(.width(3)) comparator_1 (.a(in_1), .b(in_3), .eq(Rs____Rt__Ex));  // open: gt, lt
  Comparator #(.width(3)) comparator_2 (.a(in_2), .b(in_3), .eq(Rt____Rt__Ex));  // open: gt, lt
  or or_1 (or_1_out, and_1_out, Rs____Rt__Ex);
  and and_2 (out_6, or_1_out, in_4);

  // Other names for the same wires on the sheet: Mem_Read_Ex = in_4; Mem_Read_Id = in_5; Rs_Id[2:0] = in_1;
  //   Rt_Ex[2:0] = in_3; Rt_Id[2:0] = in_2; stall = out_6
endmodule
