// Logisim project ALU.circ as structural Verilog: 2 circuits, main circuit ALU
module ALU (
  input  [3:0] in_1,
  input  [15:0] in_2,
  input  [15:0] in_3,
  input  [3:0] in_4,
  output [15:0] out_5,
  output out_6,
  output out_7
);

  wire [15:0] au_1_out_4, logicunit_1_out_4, main_1_p4;

  // shifter_main main_1: pin names not known; wires that end beside it: in_2, in_4, in_1[3:2], main_1_p4
  LogicUnit logicunit_1 (.in_3(in_3), .out_4(logicunit_1_out_4), .in_2(in_2), .in_1(in_1[3:2]));
  AU au_1 (.in_1(in_1[3:2]), .in_2(in_2), .in_3(in_3), .out_4(au_1_out_4), .out_5(out_7), .out_6(out_6));
  Multiplexer #(.select(2), .width(16), .enable("false")) multiplexer_1 (
    .in0(logicunit_1_out_4), .in1(au_1_out_4), .in2(main_1_p4), .out(out_5), .sel(in_1[1:0]));  // open: in3

  // Other names for the same wires on the sheet: selector[1:0] = in_1[1:0]; operation[1:0] = in_1[3:2];
  //   input_1[15:0] = in_2; input_2[15:0] = in_3; output[15:0] = out_5; over_flow = out_7; shift_amount[3:0] = in_4;
  //   zero = out_6
endmodule

module ALU_TEST (
  input  [3:0] in_1,
  input  [15:0] in_2,
  input  [15:0] in_3,
  input  [3:0] in_4,
  output [15:0] out_5
);

  ALU alu_1 (.in_1(in_1), .in_2(in_2), .in_3(in_3), .in_4(in_4), .out_5(out_5));  // open: out_6, out_7
endmodule
