// Logisim project logicUnit.circ as structural Verilog: 1 circuit, main circuit LogicUnit
module LogicUnit (
  input  [15:0] in_1,
  input  [15:0] in_2,
  input  [1:0] in_3,
  output [15:0] out_4
);

  wire [15:0] AND, NOR, OR, XOR;

  assign AND = in_1 & in_2;  // AND_Gate and_1, 16 bits wide
  assign OR = in_1 | in_2;  // OR_Gate or_1, 16 bits wide
  assign XOR = in_1 ^ in_2;  // XOR_Gate xor_1, 16 bits wide
  assign NOR = ~(in_1 | in_2);  // NOR_Gate nor_1, 16 bits wide
  Multiplexer #(.select(2), .width(16), .disabled(0), .enable("false")) multiplexer_1 (
    .in0(AND), .in1(OR), .in2(XOR), .in3(NOR), .out(out_4), .sel(in_3));

  // Other names for the same wires on the sheet: A[15:0] = in_1; B[15:0] = in_2; OPR[1:0] = in_3; OUT[15:0] = out_4
endmodule
