// Logisim project Forward Unit.circ as structural Verilog: 4 circuits, main circuit Forwarding Unit
module Forwarding_Unit (
  input  [2:0] in_1,
  input  [2:0] in_2,
  input  in_3,
  input  [2:0] in_4,
  input  in_5,
  input  [2:0] in_6,
  output [1:0] out_7,
  output [1:0] out_8,
  output out_9
);

  Forwarding_A forwarding_a_1 (.in_1(in_1), .in_2(in_3), .in_3(in_4), .in_4(in_5), .in_5(in_6), .out_6(out_7));
  Forwarding_B forwarding_b_1 (.in_1(in_2), .in_2(in_3), .in_3(in_4), .in_4(in_5), .in_5(in_6), .out_6(out_8));
  StForward stforward_1 (.in_1(in_2), .in_2(in_3), .in_3(in_4), .out_4(out_9));

  // Other names for the same wires on the sheet: Foeward_A[1:0] = out_7; Foeward_B[1:0] = out_8;
  //   Forward_Store = out_9; RegDes_Ex_Mem[2:0] = in_4; RegDes_Mem_WB[2:0] = in_6; RegWr_Ex_Mem = in_3;
  //   RegWr_Mem_WB = in_5; Rs_Id_Ex[2:0] = in_1; Rt_Id_Ex[2:0] = in_2
endmodule

module Forwarding_A (
  input  [2:0] in_1,
  input  in_2,
  input  [2:0] in_3,
  input  in_4,
  input  [2:0] in_5,
  output [1:0] out_6
);

  wire comparator_1_eq, comparator_2_eq, Rd1____0, Rd2____0, Rs____RegDes_Ex_Mem, Rs____RegDes_Mem_WB;

  Multiplexer #(.select(2), .width(2), .enable("false")) multiplexer_1 (
    .in0(2'b00), .in1(2'b01), .in2(2'b10), .in3(2'b10), .out(out_6),
    .sel({Rs____RegDes_Ex_Mem, Rs____RegDes_Mem_WB}));
  Comparator #(.width(3)) comparator_1 (.a(in_1), .b(in_3), .eq(comparator_1_eq));  // open: gt, lt
  Comparator #(.width(3)) comparator_2 (.a(in_1), .b(in_5), .eq(comparator_2_eq));  // open: gt, lt
  and and_1 (Rs____RegDes_Ex_Mem, in_2, comparator_1_eq, Rd1____0);
  and and_2 (Rs____RegDes_Mem_WB, in_4, comparator_2_eq, Rd2____0);
  or or_1 (Rd1____0, in_3[2], in_3[1], in_3[0]);
  or or_2 (Rd2____0, in_5[2], in_5[1], in_5[0]);

  // Other names for the same wires on the sheet: ForwardSignal[1:0] = out_6; RegDes_Ex_Mem[2:0] = in_3;
  //   RegDes_Mem_WB[2:0] = in_5; RegWr_Ex_Mem = in_2; RegWr_Mem_WB = in_4; Rs_Id_Ex[2:0] = in_1
endmodule

module Forwarding_B (
  input  [2:0] in_1,
  input  in_2,
  input  [2:0] in_3,
  input  in_4,
  input  [2:0] in_5,
  output [1:0] out_6
);

  wire comparator_1_eq, comparator_2_eq, Rd1____0, Rd2____0, Rt____RegDes_Ex_Mem, Rt____RegDes_Mem_WB;

  Multiplexer #(.select(2), .width(2), .enable("false")) multiplexer_1 (
    .in0(2'b00), .in1(2'b01), .in2(2'b10), .in3(2'b10), .out(out_6),
    .sel({Rt____RegDes_Ex_Mem, Rt____RegDes_Mem_WB}));
  Comparator #(.width(3)) comparator_1 (.a(in_1), .b(in_3), .eq(comparator_1_eq));  // open: gt, lt
  Comparator #(.width(3)) comparator_2 (.a(in_1), .b(in_5), .eq(comparator_2_eq));  // open: gt, lt
  and and_1 (Rt____RegDes_Ex_Mem, in_2, comparator_1_eq, Rd1____0);
  and and_2 (Rt____RegDes_Mem_WB, in_4, comparator_2_eq, Rd2____0);
  or or_1 (Rd1____0, in_3[2], in_3[1], in_3[0]);
  or or_2 (Rd2____0, in_5[2], in_5[1], in_5[0]);

  // Other names for the same wires on the sheet: ForwardSignal[1:0] = out_6; RegDes_Ex_Mem[2:0] = in_3;
  //   RegDes_Mem_WB[2:0] = in_5; RegWr_Ex_Mem = in_2; RegWr_Mem_WB = in_4; Rt_Id_Ex[2:0] = in_1
endmodule

module StForward (
  input  [2:0] in_1,
  input  in_2,
  input  [2:0] in_3,
  output out_4
);

  wire comparator_1_eq, Rd1____0, Rs____RegDes_Ex_Mem;

  Comparator #(.width(3)) comparator_1 (.a(in_1), .b(in_3), .eq(comparator_1_eq));  // open: gt, lt
  Multiplexer #(.enable("false")) multiplexer_1 (.in0(1'b0), .in1(1'b1), .out(out_4), .sel(Rs____RegDes_Ex_Mem));
  and and_1 (Rs____RegDes_Ex_Mem, in_2, comparator_1_eq, Rd1____0);
  or or_1 (Rd1____0, in_3[2], in_3[1], in_3[0]);

  // Other names for the same wires on the sheet: ForwardSignal = out_4; RegDes_Ex_Mem[2:0] = in_3;
  //   RegWr_Ex_Mem = in_2; Rt_Id_Ex[2:0] = in_1
endmodule
