// Logisim project ID Branch Forward.circ as structural Verilog: 5 circuits, main circuit MEM->ID Forward
module ID_Branch_Forward (
  input  in_1,
  input  [2:0] in_2,
  input  [2:0] in_3,
  input  [2:0] in_4,
  input  [2:0] in_5,
  input  [2:0] in_6,
  output [1:0] out_7,
  output [1:0] out_8
);

  wire ForwardC_EX, ForwardC_MEM, ForwardC_WB, ForwardD_EX, ForwardD_MEM, ForwardD_WB;

  Calc_FC_FD calc_fc_fd_1 (.EX(ForwardC_EX), .MEM(ForwardC_MEM), .WB(ForwardC_WB), .F1(out_7[1]), .F0(out_7[0]));
  EX__ID_Forward ex_id_forward_1 (
    .in_1(in_1), .in_2(in_2), .in_3(in_5), .in_4(in_6), .out_5(ForwardC_EX), .out_6(ForwardD_EX));
  MEM__ID_Forward mem_id_forward_1 (
    .in_1(in_1), .in_2(in_3), .in_3(in_5), .in_4(in_6), .out_5(ForwardC_MEM), .out_6(ForwardD_MEM));
  WB__ID_Forward wb_id_forward_1 (
    .in_1(in_1), .in_2(in_4), .in_3(in_5), .in_4(in_6), .out_5(ForwardC_WB), .out_6(ForwardD_WB));
  Calc_FC_FD calc_fc_fd_2 (.EX(ForwardD_EX), .MEM(ForwardD_MEM), .WB(ForwardD_WB), .F1(out_8[1]), .F0(out_8[0]));

  // Other names for the same wires on the sheet: Branch = in_1; EX_MEM_Rd[2:0] = in_3; ForwardC[1:0] = out_7;
  //   ForwardD[1:0] = out_8; ID_EX_Rd[2:0] = in_2; IF_ID_Rs[2:0] = in_5; IF_ID_Rt[2:0] = in_6; MEM_WB_Rd[2:0] = in_4
endmodule

module EX__ID_Forward (
  input  in_1,
  input  [2:0] in_2,
  input  [2:0] in_3,
  input  [2:0] in_4,
  output out_5,
  output out_6
);

  wire nR0, Rd__Rs, Rd__Rt;

  and and_1 (out_5, in_1, nR0, Rd__Rs);
  or or_1 (nR0, in_2[0], in_2[1], in_2[2]);
  Comparator #(.width(3)) comparator_1 (.a(in_2), .b(in_3), .eq(Rd__Rs));  // open: gt, lt
  Comparator #(.width(3)) comparator_2 (.a(in_2), .b(in_4), .eq(Rd__Rt));  // open: gt, lt
  and and_2 (out_6, in_1, nR0, Rd__Rt);

  // Other names for the same wires on the sheet: Branch = in_1; ForwardC_EX = out_5; ForwardD_EX = out_6;
  //   ID_EX_Rd[2:0] = in_2; IF_ID_Rs[2:0] = in_3; IF_ID_Rt[2:0] = in_4
endmodule

module MEM__ID_Forward (
  input  in_1,
  input  [2:0] in_2,
  input  [2:0] in_3,
  input  [2:0] in_4,
  output out_5,
  output out_6
);

  wire nR0, Rd__Rs, Rd__Rt;

  and and_1 (out_5, in_1, nR0, Rd__Rs);
  or or_1 (nR0, in_2[0], in_2[1], in_2[2]);
  Comparator #(.width(3)) comparator_1 (.a(in_2), .b(in_3), .eq(Rd__Rs));  // open: gt, lt
  Comparator #(.width(3)) comparator_2 (.a(in_2), .b(in_4), .eq(Rd__Rt));  // open: gt, lt
  and and_2 (out_6, in_1, nR0, Rd__Rt);

  // Other names for the same wires on the sheet: Branch = in_1; EX_MEM_Rd[2:0] = in_2; ForwardC_MEM = out_5;
  //   ForwardD_MEM = out_6; IF_ID_Rs[2:0] = in_3; IF_ID_Rt[2:0] = in_4
endmodule

module WB__ID_Forward (
  input  in_1,
  input  [2:0] in_2,
  input  [2:0] in_3,
  input  [2:0] in_4,
  output out_5,
  output out_6
);

  wire nR0, Rd__Rs, Rd__Rt;

  and and_1 (out_5, in_1, nR0, Rd__Rs);
  or or_1 (nR0, in_2[0], in_2[1], in_2[2]);
  Comparator #(.width(3)) comparator_1 (.a(in_2), .b(in_3), .eq(Rd__Rs));  // open: gt, lt
  Comparator #(.width(3)) comparator_2 (.a(in_2), .b(in_4), .eq(Rd__Rt));  // open: gt, lt
  and and_2 (out_6, in_1, nR0, Rd__Rt);

  // Other names for the same wires on the sheet: Branch = in_1; ForwardC_WB = out_5; ForwardD_WB = out_6;
  //   IF_ID_Rs[2:0] = in_3; IF_ID_Rt[2:0] = in_4; MEM_WB_Rd[2:0] = in_2
endmodule

module Calc_FC_FD (
  input  EX,
  input  MEM,
  input  WB,
  output F1,
  output F0
);

  wire and_1_out, and_2_out, and_3_out, not_1_out, not_2_out, not_3_out;

  not not_1 (not_1_out, EX);
  not not_2 (not_2_out, EX);
  not not_3 (not_3_out, MEM);
  and and_1 (and_1_out, not_1_out, WB);
  and and_2 (and_2_out, not_2_out, MEM);
  and and_3 (and_3_out, not_3_out, WB);
  or or_1 (F1, and_1_out, and_2_out);
  or or_2 (F0, and_3_out, EX);
endmodule
