// Logisim project Full Circuit.circ as structural Verilog: 1 circuit, main circuit Full Circuit
module Full_Circuit (
);

  wire ALUsrc_Ex, ALUsrc_Id, Branch_J_Kill, CLK, Ext_Control_Ex, Ext_Control_Id, forwarding_unit_1_out_9,
       MemRead_Ex, MemRead_Id, MemRead_Mem, MemRead_Wb, MemWrite_Ex, MemWrite_Id, MemWrite_Mem,
       multiplexer_3_out, multiplexer_4_out, not_1_out, not_2_out, or_1_out, Overflow, RegWrite_Ex,
       RegWrite_Id, RegWrite_Mem, RegWrite_Wb, stall, zero;
  wire [1:0] F_Id, F_If, Forward_A, Forward_B, MemToReg_Ex, MemToReg_Id, MemToReg_Mem, MemToReg_Wb,
       RegDst_Signal_Id;
  wire [2:0] Rd_Id, Rd_If, RegDes_Ex, RegDes_Id, RegDes_Mem, RegDes_Wb, Rs_Ex, Rs_Id, Rs_If, Rs_Mem, Rt_Ex,
       Rt_Id, Rt_If, Rt_Mem;
  wire [3:0] ALUop_Ex, ALUop_Id, PCsrc_Id, Shift_Amount_Ex, Shift_Amount_Id, Shift_Amount_If;
  wire [4:0] Imm_5_Id, Imm_5_If, OP_Id, OP_If;
  wire [10:0] Imm_11_Id, Imm_11_If;
  wire [15:0] ALU_out_Ex, ALU_out_Mem, ALU_out_Wb, bit_extender_1_out, Ext_Out_Ex, Ext_Out_Id, Imm_11__5_Ex,
       Imm_11__5_Id, Imm_11__5_Mem, Imm_11__5_Wb, ins_Id, ins_If, Mem_out_Mem, Mem_out_Wb, multiplexer_1_out,
       multiplexer_5_out, multiplexer_6_out, multiplexer_7_out, multiplexer_8_out, multiplexer_9_out,
       multiplexer_10_out, multiplexer_11_out, Next_PC, PC_1_Ex, PC_1_Id, PC_1_If, PC_1_Mem, PC_1_Wb, PC_Id,
       PC_If, R1, R2, R3, R4, R5, R6, R7, Rs_Data_Ex, Rs_Data_Id, Rs_Data_Mem, Rt_Data_Ex, Rt_Data_Id,
       Rt_Data_Mem, Write_Data;

  Adder #(.width(16)) adder_1 (.a(PC_If), .b(16'h1), .out(PC_1_If));  // open: cin, cout
  // Probe on R1
  Multiplexer #(.width(16), .enable("false")) multiplexer_1 (
    .in0(PC_1_If), .in1(Next_PC), .out(multiplexer_1_out), .sel(Branch_J_Kill));
  Clock clock_1 (.out(CLK));
  // Probe on R2
  // Probe on PC_If
  // Probe on ins_If
  Register #(.width(16)) PC (.D(multiplexer_1_out), .en(not_1_out), .Q(PC_If), .clk(CLK));  // open: clr
  not not_1 (not_1_out, stall);
  // Probe on R3
  // Probe on R4
  // Probe on R5
  InstructionMemory_main main_1 (
    .PC_Address(PC_If), .out_2(Rt_If), .out_3(Rs_If), .out_5(Rd_If), .out_6(F_If), .out_7(OP_If),
    .out_8(Imm_5_If), .out_10(Imm_11_If), .out_9(Shift_Amount_If), .out_4(ins_If));
  // Probe on R6
  // Probe on R7
  or or_1 (or_1_out, stall, Branch_J_Kill);
  Reg_If_Id reg_if_id_1 (
    .in_3(PC_If), .in_4(F_If), .in_5(Rt_If), .in_6(OP_If), .in_7(Rs_If), .in_8(Imm_5_If), .in_9(Rd_If),
    .in_10(Imm_11_If), .in_11(Shift_Amount_If), .in_12(ins_If), .out_14(PC_Id), .out_15(F_Id),
    .out_16(Rt_Id), .out_17(OP_Id), .out_18(Rs_Id), .out_19(Imm_5_Id), .out_20(Rd_Id), .out_21(Imm_11_Id),
    .out_22(Shift_Amount_Id), .out_23(ins_Id), .in_1(CLK), .in_13(PC_1_If), .out_24(PC_1_Id), .in_2(or_1_out));
  Multiplexer #(.select(2), .width(3), .enable("false")) multiplexer_2 (
    .in0(Rt_Id), .in1(Rd_Id), .in2(3'b001), .in3(3'b111), .out(RegDes_Id), .sel(RegDst_Signal_Id));
  Control_Unit control_unit_1 (
    .in_1(OP_Id), .in_2(F_Id), .out_4(ALUsrc_Id), .out_3(ALUop_Id), .out_5(MemRead_Id), .out_6(MemWrite_Id),
    .out_7(Ext_Control_Id), .out_8(MemToReg_Id), .out_9(RegWrite_Id), .out_10(RegDst_Signal_Id),
    .out_11(PCsrc_Id));
  not not_2 (not_2_out, CLK);
  Hazard_Detection_Unit hazard_detection_unit_1 (
    .in_1(Rs_Id), .in_2(Rt_Id), .in_3(Rt_Ex), .in_4(MemRead_Ex), .out_5(stall));
  RegFile regfile_1 (
    .out_7(Rs_Data_Id), .in_2(Rs_Id), .in_6(not_2_out), .out_8(Rt_Data_Id), .in_3(Rt_Id), .in_5(RegWrite_Wb),
    .in_4(RegDes_Wb), .in_1(Write_Data), .out_9(R1), .out_10(R2), .out_11(R3), .out_12(R4), .out_13(R5),
    .out_14(R6), .out_15(R7));
  PC_control pc_control_1 (
    .in_1(PC_Id), .in_2(PCsrc_Id), .in_5(Imm_11_Id), .in_6(Imm_5_Id), .out_7(Next_PC), .in_3(Rs_Data_Id),
    .in_4(Rs_Data_Id), .out_8(Branch_J_Kill));
  assign bit_extender_1_out = {{5{1'b0}}, Imm_11_Id};  // Bit_Extender bit_extender_1
  Extender extender_1 (.in_1(Ext_Control_Id), .in_2(Imm_5_Id), .out_3(Ext_Out_Id));
  Shifter #(.width(16)) shifter_1 (.in(bit_extender_1_out), .\dist (4'b0101), .out(Imm_11__5_Id));
  Multiplexer #(.enable("false")) multiplexer_3 (.in0(RegWrite_Id), .in1(1'b0), .out(multiplexer_3_out), .sel(stall));
  Multiplexer #(.enable("false")) multiplexer_4 (.in0(MemWrite_Id), .in1(1'b0), .out(multiplexer_4_out), .sel(stall));
  Reg_Id_Ex reg_id_ex_1 (
    .in_3(ALUop_Id), .in_4(ALUsrc_Id), .in_5(MemRead_Id), .in_6(multiplexer_4_out), .in_7(Ext_Control_Id),
    .in_8(MemToReg_Id), .in_9(Rs_Data_Id), .in_10(Rt_Data_Id), .out_19(ALUop_Ex), .out_20(ALUsrc_Ex),
    .out_21(MemRead_Ex), .out_22(MemWrite_Ex), .out_23(Ext_Control_Ex), .out_24(MemToReg_Ex),
    .out_25(Rs_Data_Ex), .out_26(Rt_Data_Ex), .in_1(CLK), .in_15(Rs_Id), .out_31(Rs_Ex), .in_16(Rt_Id),
    .out_32(Rt_Ex), .in_17(RegDes_Id), .out_33(RegDes_Ex), .in_14(multiplexer_3_out), .out_30(RegWrite_Ex),
    .in_12(Ext_Out_Id), .out_28(Ext_Out_Ex), .in_11(Shift_Amount_Id), .out_27(Shift_Amount_Ex),
    .in_13(Imm_11__5_Id), .out_29(Imm_11__5_Ex), .in_2(PC_1_Id), .out_18(PC_1_Ex));
  Multiplexer #(.width(16), .enable("false")) multiplexer_5 (
    .in0(ALU_out_Mem), .in1(Mem_out_Mem), .out(multiplexer_5_out), .sel(MemRead_Mem));
  Multiplexer #(.width(16), .enable("false")) multiplexer_6 (
    .in0(ALU_out_Wb), .in1(Mem_out_Wb), .out(multiplexer_6_out), .sel(MemRead_Wb));
  Multiplexer #(.select(2), .width(16), .enable("false")) multiplexer_7 (
    .in0(Rt_Data_Ex), .in1(multiplexer_6_out), .in2(multiplexer_5_out), .out(multiplexer_7_out),
    .sel(Forward_B));  // open: in3
  Multiplexer #(.width(16), .enable("false")) multiplexer_8 (
    .in0(multiplexer_7_out), .in1(Ext_Out_Ex), .out(multiplexer_8_out), .sel(ALUsrc_Ex));
  Multiplexer #(.select(2), .width(16), .enable("false")) multiplexer_9 (
    .in0(Rs_Data_Ex), .in1(multiplexer_6_out), .in2(multiplexer_5_out), .out(multiplexer_9_out),
    .sel(Forward_A));  // open: in3
  ALU alu_1 (
    .in_1(ALUop_Ex), .in_2(multiplexer_9_out), .in_3(multiplexer_8_out), .in_4(Shift_Amount_Ex),
    .out_5(ALU_out_Ex), .out_6(zero), .out_7(Overflow));
  Forwarding_Unit forwarding_unit_1 (
    .in_1(Rs_Ex), .in_2(Rt_Ex), .in_3(RegWrite_Mem), .in_4(RegDes_Mem), .in_5(RegWrite_Wb), .in_6(RegDes_Wb),
    .out_7(Forward_A), .out_8(Forward_B), .out_9(forwarding_unit_1_out_9));
  Multiplexer #(.width(16), .enable("false")) multiplexer_10 (
    .in0(Rt_Data_Ex), .in1(ALU_out_Mem), .out(multiplexer_10_out), .sel(forwarding_unit_1_out_9));
  Multiplexer #(.select(2), .width(16), .enable("false")) multiplexer_11 (
    .in0(ALU_out_Ex), .in1(ALU_out_Ex), .in2(Imm_11__5_Ex), .in3(PC_1_Ex), .out(multiplexer_11_out),
    .sel(MemToReg_Ex));
  Reg_Ex_Mem reg_ex_mem_1 (
    .in_1(CLK), .in_2(MemRead_Ex), .in_3(MemWrite_Ex), .in_4(multiplexer_10_out), .in_5(MemToReg_Ex),
    .in_6(Rs_Data_Ex), .in_8(RegWrite_Ex), .in_9(Rs_Ex), .in_10(Rt_Ex), .in_11(RegDes_Ex),
    .out_14(MemRead_Mem), .out_15(MemWrite_Mem), .out_16(Rt_Data_Mem), .out_17(MemToReg_Mem),
    .out_18(Rs_Data_Mem), .out_20(RegWrite_Mem), .out_21(Rs_Mem), .out_22(Rt_Mem), .out_23(RegDes_Mem),
    .in_7(multiplexer_11_out), .out_19(ALU_out_Mem), .in_12(PC_1_Ex), .out_24(PC_1_Mem),
    .in_13(Imm_11__5_Ex), .out_25(Imm_11__5_Mem));
  Data_Memory data_memory_1 (
    .Address(ALU_out_Mem), .Data_In(Rt_Data_Mem), .MemWrite(MemWrite_Mem), .MemRead(MemRead_Mem), .CLK(CLK),
    .Data_Out(Mem_out_Mem));
  Reg_Mem_Wb reg_mem_wb_1 (
    .in_1(CLK), .in_3(MemToReg_Mem), .in_4(ALU_out_Mem), .in_5(PC_1_Mem), .in_6(Imm_11__5_Mem),
    .in_7(Mem_out_Mem), .out_11(MemToReg_Wb), .out_12(ALU_out_Wb), .out_13(PC_1_Wb), .out_14(Imm_11__5_Wb),
    .out_15(Mem_out_Wb), .in_8(RegWrite_Mem), .out_16(RegWrite_Wb), .in_9(RegDes_Mem), .out_17(RegDes_Wb),
    .in_2(MemRead_Mem), .out_10(MemRead_Wb));
  Multiplexer #(.select(2), .width(16), .enable("false")) multiplexer_12 (
    .in0(ALU_out_Wb), .in1(Mem_out_Wb), .in2(Imm_11__5_Wb), .in3(PC_1_Wb), .out(Write_Data), .sel(MemToReg_Wb));
endmodule
