// Logisim project InstructionDecoder.circ as structural Verilog: 1 circuit, main circuit InstructionDecoder
module InstructionDecoder (
  input  [15:0] Instruction,
  output [2:0] out_2,
  output [2:0] out_3,
  output [2:0] out_4,
  output [1:0] out_5,
  output [4:0] out_6,
  output [4:0] out_7,
  output [3:0] out_8,
  output [10:0] out_9,
  output [15:0] out_10
);


  assign out_2 = Instruction[2:0];
  assign out_3 = Instruction[5:3];
  assign out_4 = Instruction[8:6];
  assign out_5 = Instruction[10:9];
  assign out_6 = Instruction[15:11];
  assign out_7 = Instruction[10:6];
  assign out_8 = Instruction[9:6];
  assign out_9 = Instruction[10:0];
  assign out_10 = Instruction;

  // Other names for the same wires on the sheet: Imm_11[10:0] = Instruction[10:0]; Rt[2:0] = Instruction[2:0];
  //   Rs[2:0] = Instruction[5:3]; Imm_5[4:0] = Instruction[10:6]; Rd[2:0] = Instruction[8:6];
  //   Shift_amount[3:0] = Instruction[9:6]; F[1:0] = Instruction[10:9]; OP[4:0] = Instruction[15:11]
endmodule
