// Logisim project PC Control.circ as structural Verilog: 1 circuit, main circuit PC control
module PC_control (
  input  [15:0] in_1,
  input  [3:0] in_2,
  input  [15:0] in_3,
  input  [15:0] in_4,
  input  [10:0] in_5,
  input  [4:0] in_6,
  output [15:0] out_7,
  output out_8
);

  wire Branch_Taken, SLT_Flag, Zero_Flag;
  wire [15:0] adder_1_out, ALU_Result, branch_control_1_out_6, Imm_5, Imm_11;

  assign Imm_11 = {{5{in_5[10]}}, in_5};  // Bit_Extender bit_extender_1
  assign Imm_5 = {{11{in_6[4]}}, in_6};  // Bit_Extender bit_extender_2
  Comparator #(.width(16)) comparator_1 (.a(in_3), .b(in_4), .gt(SLT_Flag), .eq(Zero_Flag));  // open: lt
  Multiplexer #(.select(2), .enable("false")) multiplexer_1 (
    .in0(1'b1), .in1(1'b1), .in2(1'b1), .in3(Branch_Taken), .out(out_8), .sel(in_2[1:0]));
  Adder #(.width(16)) adder_1 (.a(in_1), .b(Imm_11), .out(adder_1_out));  // open: cin, cout
  Branch_Control branch_control_1 (
    .in_1(in_1), .in_2(Zero_Flag), .in_3(SLT_Flag), .in_4(Imm_5), .in_5(in_2[3:2]),
    .out_6(branch_control_1_out_6), .out_7(Branch_Taken));
  Multiplexer #(.select(2), .width(16), .enable("false")) multiplexer_2 (
    .in0({16{1'b1}}), .in1(ALU_Result), .in2(adder_1_out), .in3(branch_control_1_out_6), .out(out_7),
    .sel(in_2[1:0]));

  // Other names for the same wires on the sheet: Branch_J_Kill = out_8; Current_PC[15:0] = in_1;
  //   PC_Src[1:0] = in_2[1:0]; Branch_Op[1:0] = in_2[3:2]; Next_PC[15:0] = out_7; Rs[15:0] = in_3; Rt[15:0] = in_4
endmodule
