// Logisim project Piplining Registers.circ as structural Verilog: 4 circuits, main circuit Reg If/Id
module Reg_If_Id (
  input  in_1,
  input  in_2,
  input  [15:0] in_3,
  input  [1:0] in_4,
  input  [2:0] in_5,
  input  [4:0] in_6,
  input  [2:0] in_7,
  input  [4:0] in_8,
  input  [2:0] in_9,
  input  [10:0] in_10,
  input  [3:0] in_11,
  input  [15:0] in_12,
  input  [15:0] in_13,
  output [15:0] out_14,
  output [1:0] out_15,
  output [2:0] out_16,
  output [4:0] out_17,
  output [2:0] out_18,
  output [4:0] out_19,
  output [2:0] out_20,
  output [10:0] out_21,
  output [3:0] out_22,
  output [15:0] out_23,
  output [15:0] out_24
);

  wire Disable;

  not not_1 (Disable, in_2);
  Register #(.width(16)) PC (.D(in_3), .en(Disable), .Q(out_14), .clk(in_1));  // open: clr
  Register #(.width(3)) Rt (.D(in_5), .en(Disable), .Q(out_16), .clk(in_1));  // open: clr
  Register #(.width(3)) Rs (.D(in_7), .en(Disable), .Q(out_18), .clk(in_1));  // open: clr
  Register #(.width(3)) Rd (.D(in_9), .en(Disable), .Q(out_20), .clk(in_1));  // open: clr
  Register #(.width(4)) Shift_amount (.D(in_11), .en(Disable), .Q(out_22), .clk(in_1));  // open: clr
  Register #(.width(16)) Pc_1 (.D(in_13), .en(Disable), .Q(out_24), .clk(in_1));  // open: clr
  Register #(.width(2)) F (.D(in_4), .en(Disable), .Q(out_15), .clk(in_1));  // open: clr
  Register #(.width(5)) OP (.D(in_6), .en(Disable), .Q(out_17), .clk(in_1));  // open: clr
  Register #(.width(5)) Imm_5 (.D(in_8), .en(Disable), .Q(out_19), .clk(in_1));  // open: clr
  Register #(.width(11)) Imm_11 (.D(in_10), .en(Disable), .Q(out_21), .clk(in_1));  // open: clr
  Register #(.width(16)) Ins (.D(in_12), .en(Disable), .Q(out_23), .clk(in_1));  // open: clr

  // Other names for the same wires on the sheet: CLK = in_1
endmodule

module Reg_Id_Ex (
  input  in_1,
  input  [15:0] in_2,
  input  [3:0] in_3,
  input  in_4,
  input  in_5,
  input  in_6,
  input  in_7,
  input  [1:0] in_8,
  input  [15:0] in_9,
  input  [15:0] in_10,
  input  [3:0] in_11,
  input  [15:0] in_12,
  input  [15:0] in_13,
  input  in_14,
  input  [2:0] in_15,
  input  [2:0] in_16,
  input  [2:0] in_17,
  output [15:0] out_18,
  output [3:0] out_19,
  output out_20,
  output out_21,
  output out_22,
  output out_23,
  output [1:0] out_24,
  output [15:0] out_25,
  output [15:0] out_26,
  output [3:0] out_27,
  output [15:0] out_28,
  output [15:0] out_29,
  output out_30,
  output [2:0] out_31,
  output [2:0] out_32,
  output [2:0] out_33
);

  Register #(.width(4)) ALUop (.D(in_3), .Q(out_19), .clk(in_1));  // open: en, clr
  Register #(.width(1)) MemRead (.D(in_5), .Q(out_21), .clk(in_1));  // open: en, clr
  Register #(.width(1)) Ext_Control (.D(in_7), .Q(out_23), .clk(in_1));  // open: en, clr
  Register #(.width(16)) Rs_Data (.D(in_9), .Q(out_25), .clk(in_1));  // open: en, clr
  Register #(.width(4)) Shift_Amount (.D(in_11), .Q(out_27), .clk(in_1));  // open: en, clr
  Register #(.width(1)) RegWrite (.D(in_14), .Q(out_30), .clk(in_1));  // open: en, clr
  Register #(.width(3)) Rt (.D(in_16), .Q(out_32), .clk(in_1));  // open: en, clr
  Register #(.width(16)) PC (.D(in_2), .Q(out_18), .clk(in_1));  // open: en, clr
  Register #(.width(1)) ALUsrc (.D(in_4), .Q(out_20), .clk(in_1));  // open: en, clr
  Register #(.width(1)) MemWrite (.D(in_6), .Q(out_22), .clk(in_1));  // open: en, clr
  Register #(.width(2)) MemToReg (.D(in_8), .Q(out_24), .clk(in_1));  // open: en, clr
  Register #(.width(16)) Rt_Data (.D(in_10), .Q(out_26), .clk(in_1));  // open: en, clr
  Register #(.width(16)) Ex_Out (.D(in_12), .Q(out_28), .clk(in_1));  // open: en, clr
  Register #(.width(16)) Imm_11__5 (.D(in_13), .Q(out_29), .clk(in_1));  // open: en, clr
  Register #(.width(3)) Rs (.D(in_15), .Q(out_31), .clk(in_1));  // open: en, clr
  Register #(.width(3)) Rd (.D(in_17), .Q(out_33), .clk(in_1));  // open: en, clr

  // Other names for the same wires on the sheet: CLK = in_1
endmodule

module Reg_Ex_Mem (
  input  in_1,
  input  in_2,
  input  in_3,
  input  [15:0] in_4,
  input  [1:0] in_5,
  input  [15:0] in_6,
  input  [15:0] in_7,
  input  in_8,
  input  [2:0] in_9,
  input  [2:0] in_10,
  input  [2:0] in_11,
  input  [15:0] in_12,
  input  [15:0] in_13,
  output out_14,
  output out_15,
  output [15:0] out_16,
  output [1:0] out_17,
  output [15:0] out_18,
  output [15:0] out_19,
  output out_20,
  output [2:0] out_21,
  output [2:0] out_22,
  output [2:0] out_23,
  output [15:0] out_24,
  output [15:0] out_25
);

  Register #(.width(1)) MemRead (.D(in_2), .Q(out_14), .clk(in_1));  // open: en, clr
  Register #(.width(16)) Rt_Data (.D(in_4), .Q(out_16), .clk(in_1));  // open: en, clr
  Register #(.width(16)) Rs_Data (.D(in_6), .Q(out_18), .clk(in_1));  // open: en, clr
  Register #(.width(1)) RegWrite (.D(in_8), .Q(out_20), .clk(in_1));  // open: en, clr
  Register #(.width(3)) Rt (.D(in_10), .Q(out_22), .clk(in_1));  // open: en, clr
  Register #(.width(16)) PC (.D(in_12), .Q(out_24), .clk(in_1));  // open: en, clr
  Register #(.width(1)) MemWrite (.D(in_3), .Q(out_15), .clk(in_1));  // open: en, clr
  Register #(.width(2)) MemToReg (.D(in_5), .Q(out_17), .clk(in_1));  // open: en, clr
  Register #(.width(3)) Rd (.D(in_11), .Q(out_23), .clk(in_1));  // open: en, clr
  Register #(.width(16)) ALU_OUT (.D(in_7), .Q(out_19), .clk(in_1));  // open: en, clr
  Register #(.width(3)) Rs (.D(in_9), .Q(out_21), .clk(in_1));  // open: en, clr
  Register #(.width(16)) Imm_11__5 (.D(in_13), .Q(out_25), .clk(in_1));  // open: en, clr

  // Other names for the same wires on the sheet: CLK = in_1
endmodule

module Reg_Mem_Wb (
  input  in_1,
  input  in_2,
  input  [1:0] in_3,
  input  [15:0] in_4,
  input  [15:0] in_5,
  input  [15:0] in_6,
  input  [15:0] in_7,
  input  in_8,
  input  [2:0] in_9,
  output out_10,
  output [1:0] out_11,
  output [15:0] out_12,
  output [15:0] out_13,
  output [15:0] out_14,
  output [15:0] out_15,
  output out_16,
  output [2:0] out_17
);

  Register #(.width(1)) RegWrite (.D(in_8), .Q(out_16), .clk(in_1));  // open: en, clr
  Register #(.width(16)) PC (.D(in_5), .Q(out_13), .clk(in_1));  // open: en, clr
  Register #(.width(1)) MemRead (.D(in_2), .Q(out_10), .clk(in_1));  // open: en, clr
  Register #(.width(2)) MemToReg (.D(in_3), .Q(out_11), .clk(in_1));  // open: en, clr
  Register #(.width(16)) Mem_OUT (.D(in_7), .Q(out_15), .clk(in_1));  // open: en, clr
  Register #(.width(3)) Rd (.D(in_9), .Q(out_17), .clk(in_1));  // open: en, clr
  Register #(.width(16)) ALU_OUT (.D(in_4), .Q(out_12), .clk(in_1));  // open: en, clr
  Register #(.width(16)) Imm_11__5 (.D(in_6), .Q(out_14), .clk(in_1));  // open: en, clr

  // Other names for the same wires on the sheet: CLK = in_1
endmodule
