// Logisim project Register Piplining.circ as structural Verilog: 1 circuit, main circuit Reg If/Id
module Reg_If_Id (
  input  [15:0] in_1,
  input  [1:0] in_2,
  input  [2:0] in_3,
  input  [4:0] in_4,
  input  [2:0] in_5,
  input  [4:0] in_6,
  input  [2:0] in_7,
  input  [10:0] in_8,
  input  [3:0] in_9,
  input  [15:0] in_10,
  output [15:0] out_11,
  output [1:0] out_12,
  output [2:0] out_13,
  output [4:0] out_14,
  output [2:0] out_15,
  output [4:0] out_16,
  output [2:0] out_17,
  output [10:0] out_18,
  output [3:0] out_19,
  output [15:0] out_20
);

  wire CLK;

  Clock clock_1 (.out(CLK));
  Register #(.width(16)) Pc_1 (.D(in_1), .Q(out_11), .clk(CLK));  // open: en, clr
  Register #(.width(3)) Rt (.D(in_3), .Q(out_13), .clk(CLK));  // open: en, clr
  Register #(.width(3)) Rs (.D(in_5), .Q(out_15), .clk(CLK));  // open: en, clr
  Register #(.width(3)) Rd (.D(in_7), .Q(out_17), .clk(CLK));  // open: en, clr
  Register #(.width(4)) Shift_amount (.D(in_9), .Q(out_19), .clk(CLK));  // open: en, clr
  Register #(.width(2)) F (.D(in_2), .Q(out_12), .clk(CLK));  // open: en, clr
  Register #(.width(5)) OP (.D(in_4), .Q(out_14), .clk(CLK));  // open: en, clr
  Register #(.width(5)) Imm_5 (.D(in_6), .Q(out_16), .clk(CLK));  // open: en, clr
  Register #(.width(11)) Imm_11 (.D(in_8), .Q(out_18), .clk(CLK));  // open: en, clr
  Register #(.width(16)) Ins (.D(in_10), .Q(out_20), .clk(CLK));  // open: en, clr
endmodule
