// Logisim project Register File.circ as structural Verilog: 1 circuit, main circuit main
module main (
  input  [2:0] in_1,
  input  [2:0] in_2,
  input  [2:0] in_3,
  input  [15:0] in_4,
  input  in_5,
  output [15:0] out_6,
  output [15:0] out_7
);

  wire and_1_out, and_2_out, and_3_out, and_4_out, and_5_out, and_6_out, and_7_out, clock_1_out, En__1,
       En__2, En__3, En__4, En__5, En__6, En__7;
  wire [15:0] D__0, D__1, D__2, D__3, D__4, D__5, D__6, D__7;

  and and_1 (and_1_out, in_5, En__1);
  and and_2 (and_2_out, in_5, En__2);
  and and_3 (and_3_out, in_5, En__3);
  and and_4 (and_4_out, in_5, En__4);
  and and_5 (and_5_out, in_5, En__5);
  and and_6 (and_6_out, in_5, En__6);
  and and_7 (and_7_out, in_5, En__7);
  Register #(.width(16)) Zero (.D({16{1'b0}}), .en(1'b0), .Q(D__0), .clk(clock_1_out));  // open: clr
  Register #(.width(16)) _1 (.D(in_4), .en(and_1_out), .Q(D__1), .clk(clock_1_out));  // open: clr
  Register #(.width(16)) _2 (.D(in_4), .en(and_2_out), .Q(D__2), .clk(clock_1_out));  // open: clr
  Register #(.width(16)) _3 (.D(in_4), .en(and_3_out), .Q(D__3), .clk(clock_1_out));  // open: clr
  Register #(.width(16)) _4 (.D(in_4), .en(and_4_out), .Q(D__4), .clk(clock_1_out));  // open: clr
  Register #(.width(16)) _5 (.D(in_4), .en(and_5_out), .Q(D__5), .clk(clock_1_out));  // open: clr
  Register #(.width(16)) _6 (.D(in_4), .en(and_6_out), .Q(D__6), .clk(clock_1_out));  // open: clr
  Register #(.width(16)) _7 (.D(in_4), .en(and_7_out), .Q(D__7), .clk(clock_1_out));  // open: clr
  Multiplexer #(.select(3), .width(16)) multiplexer_1 (
    .in0(D__0), .in1(D__1), .in2(D__2), .in3(D__3), .in4(D__4), .in5(D__5), .in6(D__6), .in7(D__7),
    .out(out_6), .sel(in_1));  // open: en
  Multiplexer #(.select(3), .width(16)) multiplexer_2 (
    .in0(D__0), .in1(D__1), .in2(D__2), .in3(D__3), .in4(D__4), .in5(D__5), .in6(D__6), .in7(D__7),
    .out(out_7), .sel(in_2));  // open: en
  Decoder #(.select(3)) decoder_1 (
    .out1(En__1), .out2(En__2), .out3(En__3), .out4(En__4), .out5(En__5), .out6(En__6), .out7(En__7),
    .sel(in_3));  // open: out0, en
  Clock clock_1 (.out(clock_1_out));

  // Other names for the same wires on the sheet: D_Reg_1[15:0] = out_6; D_Reg_2[15:0] = out_7; Reg_1[2:0] = in_1;
  //   Reg_2[2:0] = in_2; Reg_Wr = in_5; Write_Data[15:0] = in_4; Write_Reg[2:0] = in_3
endmodule
