// Logisim project PC Control.circ as structural Verilog: 1 circuit, main circuit PC control
module PC_control (
  input  [15:0] in_1,
  input  [3:0] in_2,
  input  in_3,
  input  [15:0] ALU_result,
  input  [10:0] in_5,
  input  [4:0] in_6,
  output [15:0] out_7,
  output [15:0] out_8
);

  wire [15:0] adder_2_out, branch_control_1_out_7, Imm_5, Imm_11;

  assign Imm_11 = {{5{in_5[10]}}, in_5};  // Bit_Extender bit_extender_1
  assign Imm_5 = {{11{in_6[4]}}, in_6};  // Bit_Extender bit_extender_2
  Adder #(.width(16)) adder_1 (.a(in_1), .b(16'h1), .out(out_8));  // open: cin, cout
  Adder #(.width(16)) adder_2 (.a(in_1), .b(Imm_11), .out(adder_2_out));  // open: cin, cout
  Branch_Control branch_control_1 (
    .in_1(in_1), .in_2(in_3), .in_3(ALU_result[0]), .in_4(Imm_5), .in_5(in_2[3:2]),
    .out_7(branch_control_1_out_7), .in_6(out_8));
  Multiplexer #(.select(2), .width(16), .enable("false")) multiplexer_1 (
    .in0(out_8), .in1(ALU_result), .in2(adder_2_out), .in3(branch_control_1_out_7), .out(out_7),
    .sel(in_2[1:0]));

  // Other names for the same wires on the sheet: Current_PC[15:0] = in_1; PC_Src[1:0] = in_2[1:0];
  //   Branch_Op[1:0] = in_2[3:2]; Next_PC[15:0] = out_7; Pc_1[15:0] = out_8; Rs[15:0] = ALU_result;
  //   SLT_Flag = ALU_result[0]; Zero_Flag = in_3
endmodule
