// Logisim project SingleCycleRISCmips.circ as structural Verilog: 1 circuit, main circuit Single Cycle circuit
module Single_Cycle_circuit (
);

  wire ALUsrc, CLK, Ext_Control, MemRead, MemWrite, Overflow, RegWrite, zero;
  wire [1:0] F, MemToReg, RegDst;
  wire [2:0] multiplexer_1_out, Rd, Rs, Rt;
  wire [3:0] ALUop, PCsrc, Shift_amount;
  wire [4:0] Imm_5, OP;
  wire [10:0] Imm_11;
  wire [15:0] ALU_out, bit_extender_1_out, Ext_Out, Imm_11__5, main_1_out_4, Mem_out, multiplexer_2_out,
       multiplexer_3_out, PC, PC_1, pc_control_1_out_7, R1, R2, R3, R4, R5, R6, R7, Rs_Data, Rt_Data;

  PC_control pc_control_1 (
    .in_1(PC), .in_2(PCsrc), .in_3(zero), .ALU_result(ALU_out), .in_5(Imm_11), .in_6(Imm_5),
    .out_7(pc_control_1_out_7));
  Control_Unit control_unit_1 (
    .in_1(OP), .in_2(F), .out_4(ALUsrc), .out_3(ALUop), .out_5(MemRead), .out_6(MemWrite),
    .out_7(Ext_Control), .out_8(MemToReg), .out_9(RegWrite), .out_10(RegDst), .out_11(PCsrc));
  Adder #(.width(16)) adder_1 (.a(PC), .b({16{1'b0}}), .out(PC_1), .cin(1'b1));  // open: cout
  Register #(.width(16)) u_PC (.D(pc_control_1_out_7), .en(1'b1), .Q(PC), .clk(CLK));  // open: clr
  // Probe on main_1_out_4
  InstructionMemory_main main_1 (
    .PC_Address(PC), .out_2(Rt), .out_3(Rs), .out_5(Rd), .out_6(F), .out_7(OP), .out_8(Imm_5),
    .out_10(Imm_11), .out_9(Shift_amount), .out_4(main_1_out_4));
  Multiplexer #(.select(2), .width(3), .enable("false")) multiplexer_1 (
    .in0(Rt), .in1(Rd), .in2(3'b001), .in3(3'b111), .out(multiplexer_1_out), .sel(RegDst));
  Multiplexer #(.select(2), .width(16), .enable("false")) multiplexer_2 (
    .in0(ALU_out), .in1(Mem_out), .in2(Imm_11__5), .in3(PC_1), .out(multiplexer_2_out), .sel(MemToReg));
  Clock clock_1 (.out(CLK));
  // Probe on PC
  // Probe on R2
  // Probe on R1
  // Probe on R3
  RegFile regfile_1 (
    .out_7(Rs_Data), .in_2(Rs), .in_6(CLK), .out_8(Rt_Data), .in_3(Rt), .in_5(RegWrite),
    .in_4(multiplexer_1_out), .in_1(multiplexer_2_out), .out_9(R1), .out_10(R2), .out_11(R3), .out_12(R4),
    .out_13(R5), .out_14(R6), .out_15(R7));
  // Probe on R4
  // Probe on ALU_out
  // Probe on R5
  // Probe on R6
  // Probe on R7
  Multiplexer #(.width(16), .enable("false")) multiplexer_3 (
    .in0(Rt_Data), .in1(Ext_Out), .out(multiplexer_3_out), .sel(ALUsrc));
  assign bit_extender_1_out = {{5{1'b0}}, Imm_11};  // Bit_Extender bit_extender_1
  Shifter #(.width(16)) shifter_1 (.in(bit_extender_1_out), .\dist (4'b0101), .out(Imm_11__5));
  ALU alu_1 (
    .in_1(ALUop), .in_2(Rs_Data), .in_3(multiplexer_3_out), .in_4(Shift_amount), .out_5(ALU_out),
    .out_6(zero), .out_7(Overflow));
  Extender extender_1 (.in_1(Ext_Control), .in_2(Imm_5), .out_3(Ext_Out));
  Data_Memory data_memory_1 (
    .Address(ALU_out), .Data_In(Rt_Data), .MemWrite(MemWrite), .MemRead(MemRead), .CLK(CLK),
    .Data_Out(Mem_out));
endmodule
