// Logisim project extender.circ as structural Verilog: 1 circuit, main circuit Extender
module Extender (
  input  in_1,
  input  [4:0] in_2,
  output [15:0] out_3
);

  wire [15:0] bit_extender_1_out, bit_extender_2_out;

  assign bit_extender_1_out = {{11{1'b0}}, in_2};  // Bit_Extender bit_extender_1
  assign bit_extender_2_out = {{11{in_2[4]}}, in_2};  // Bit_Extender bit_extender_2
  Multiplexer #(.width(16), .enable("false")) multiplexer_1 (
    .in0(bit_extender_1_out), .in1(bit_extender_2_out), .out(out_3), .sel(in_1));

  // Other names for the same wires on the sheet: extend_control = in_1; extended_number[15:0] = out_3;
  //   input[4:0] = in_2
endmodule
