// Logisim project jump extender.circ as structural Verilog: 1 circuit, main circuit main
module main (
  input  [10:0] in_1,
  output [15:0] out_2
);

  assign out_2 = {{5{in_1[10]}}, in_1};  // Bit_Extender bit_extender_1

  // Other names for the same wires on the sheet: input[10:0] = in_1; output[15:0] = out_2
endmodule
