// Logisim project shifter.circ as structural Verilog: 1 circuit, main circuit main
module main (
  input  [2:0] in_1,
  input  [15:0] in_2,
  input  [3:0] in_3,
  output [15:0] out_4
);

  wire [15:0] ROR, SLL, SRA, SRL;

  Shifter #(.width(16)) shifter_1 (.in(in_2), .\dist (in_3), .out(SLL));
  Shifter #(.width(16), .shift("lr")) shifter_2 (.in(in_2), .\dist (in_3), .out(SRL));
  Shifter #(.width(16), .shift("ar")) shifter_3 (.in(in_2), .\dist (in_3), .out(SRA));
  Shifter #(.width(16), .shift("rr")) shifter_4 (.in(in_2), .\dist (in_3), .out(ROR));
  Multiplexer #(.select(2), .width(16)) multiplexer_1 (
    .in0(SLL), .in1(SRL), .in2(SRA), .in3(ROR), .out(out_4), .sel(in_1[1:0]));  // open: en

  // Other names for the same wires on the sheet: shift_control[1:0] = in_1[1:0]; input[15:0] = in_2;
  //   output[15:0] = out_4; shift_amount[3:0] = in_3
endmodule
